// Logisim project CSProject 2.04.circ as structural Verilog: 4 circuits, main circuit main
module main (
  input  [4:0] bus_0,
  input  bus_0_2,
  input  bus_0_3
);

  wire [4:0] random_1_out, rom_1_data;
  wire [8:0] switch_1_output, switch_1_output_2, switch_1_output_3, switch_1_output_4, switch_1_output_5,
       switch_1_output_6, switch_1_output_7, switch_1_output_8, switch_1_output_9, switch_2_output,
       switch_2_output_2, switch_2_output_3, switch_2_output_4, switch_2_output_5, switch_2_output_6,
       switch_2_output_7, switch_2_output_8, switch_2_output_9, switch_3_output, switch_3_output_2,
       switch_3_output_3, switch_3_output_4, switch_3_output_5, switch_3_output_6, switch_3_output_7,
       switch_3_output_8, switch_3_output_9, switch_4_output, switch_4_output_2, switch_4_output_3,
       switch_4_output_4, switch_4_output_5, switch_4_output_6, switch_4_output_7, switch_4_output_8,
       switch_4_output_9, switch_5_output, switch_5_output_2, switch_5_output_3, switch_5_output_4,
       switch_5_output_5, switch_5_output_6, switch_5_output_7, switch_5_output_8, switch_5_output_9,
       switch_6_output, switch_6_output_2, switch_6_output_3, switch_6_output_4, switch_6_output_5,
       switch_6_output_6, switch_6_output_7, switch_6_output_8, switch_6_output_9, switch_7_output,
       switch_7_output_2, switch_7_output_3, switch_7_output_4, switch_7_output_5, switch_7_output_6,
       switch_7_output_7, switch_7_output_8, switch_7_output_9, switch_8_output, switch_8_output_2,
       switch_8_output_3, switch_8_output_4, switch_8_output_5, switch_8_output_6, switch_8_output_7,
       switch_8_output_8, switch_8_output_9;

  Random #(.width(5)) random_1 (.clk(bus_0_3), .out(random_1_out));  // open: next, clr
  // Probe on random_1_out
  Hex_Digit_Display hex_digit_display_1 ();  // open: value, dp
  DotMatrix #(.matrixcols(9), .matrixrows(9)) dotmatrix_1 (
    .col0(switch_1_output), .col1(switch_1_output_2), .col2(switch_1_output_3), .col3(switch_1_output_4),
    .col4(switch_1_output_5), .col5(switch_1_output_6), .col6(switch_1_output_7), .col7(switch_1_output_8),
    .col8(switch_1_output_9));
  // Probe on rom_1_data
  ROM #(.dataWidth(5)) rom_1 (.addr({random_1_out, 3'b000}), .data(rom_1_data));  // open: sel
  DotMatrix #(.matrixcols(9), .matrixrows(9)) dotmatrix_2 (
    .col0(switch_2_output), .col1(switch_2_output_2), .col2(switch_2_output_3), .col3(switch_2_output_4),
    .col4(switch_2_output_5), .col5(switch_2_output_6), .col6(switch_2_output_7), .col7(switch_2_output_8),
    .col8(switch_2_output_9));
  Switch switch_1 (
    .Output(switch_1_output), .Output_2(switch_1_output_2), .Output_3(switch_1_output_3),
    .Output_4(switch_1_output_4), .Output_5(switch_1_output_5), .Output_6(switch_1_output_6),
    .Output_7(switch_1_output_7), .Output_8(switch_1_output_8), .Output_9(switch_1_output_9), .ctrl(bus_0_2),
    .Let(rom_1_data));
  DotMatrix #(.matrixcols(9), .matrixrows(9)) dotmatrix_3 (
    .col0(switch_3_output), .col1(switch_3_output_2), .col2(switch_3_output_3), .col3(switch_3_output_4),
    .col4(switch_3_output_5), .col5(switch_3_output_6), .col6(switch_3_output_7), .col7(switch_3_output_8),
    .col8(switch_3_output_9));
  Switch switch_2 (
    .Output(switch_2_output), .Output_2(switch_2_output_2), .Output_3(switch_2_output_3),
    .Output_4(switch_2_output_4), .Output_5(switch_2_output_5), .Output_6(switch_2_output_6),
    .Output_7(switch_2_output_7), .Output_8(switch_2_output_8), .Output_9(switch_2_output_9), .ctrl(bus_0_2),
    .Let(rom_1_data));
  DotMatrix #(.matrixcols(9), .matrixrows(9)) dotmatrix_4 (
    .col0(switch_4_output), .col1(switch_4_output_2), .col2(switch_4_output_3), .col3(switch_4_output_4),
    .col4(switch_4_output_5), .col5(switch_4_output_6), .col6(switch_4_output_7), .col7(switch_4_output_8),
    .col8(switch_4_output_9));
  Switch switch_3 (
    .Output(switch_3_output), .Output_2(switch_3_output_2), .Output_3(switch_3_output_3),
    .Output_4(switch_3_output_4), .Output_5(switch_3_output_5), .Output_6(switch_3_output_6),
    .Output_7(switch_3_output_7), .Output_8(switch_3_output_8), .Output_9(switch_3_output_9), .ctrl(bus_0_2),
    .Let(rom_1_data));
  DotMatrix #(.matrixcols(9), .matrixrows(9)) dotmatrix_5 (
    .col0(switch_5_output), .col1(switch_5_output_2), .col2(switch_5_output_3), .col3(switch_5_output_4),
    .col4(switch_5_output_5), .col5(switch_5_output_6), .col6(switch_5_output_7), .col7(switch_5_output_8),
    .col8(switch_5_output_9));
  Switch switch_4 (
    .Output(switch_4_output), .Output_2(switch_4_output_2), .Output_3(switch_4_output_3),
    .Output_4(switch_4_output_4), .Output_5(switch_4_output_5), .Output_6(switch_4_output_6),
    .Output_7(switch_4_output_7), .Output_8(switch_4_output_8), .Output_9(switch_4_output_9), .ctrl(bus_0_2),
    .Let(rom_1_data));
  DotMatrix #(.matrixcols(9), .matrixrows(9)) dotmatrix_6 (
    .col0(switch_6_output), .col1(switch_6_output_2), .col2(switch_6_output_3), .col3(switch_6_output_4),
    .col4(switch_6_output_5), .col5(switch_6_output_6), .col6(switch_6_output_7), .col7(switch_6_output_8),
    .col8(switch_6_output_9));
  Switch switch_5 (
    .Output(switch_5_output), .Output_2(switch_5_output_2), .Output_3(switch_5_output_3),
    .Output_4(switch_5_output_4), .Output_5(switch_5_output_5), .Output_6(switch_5_output_6),
    .Output_7(switch_5_output_7), .Output_8(switch_5_output_8), .Output_9(switch_5_output_9), .ctrl(bus_0_2),
    .Let(rom_1_data));
  DotMatrix #(.matrixcols(9), .matrixrows(9)) dotmatrix_7 (
    .col0(switch_7_output), .col1(switch_7_output_2), .col2(switch_7_output_3), .col3(switch_7_output_4),
    .col4(switch_7_output_5), .col5(switch_7_output_6), .col6(switch_7_output_7), .col7(switch_7_output_8),
    .col8(switch_7_output_9));
  Switch switch_6 (
    .Output(switch_6_output), .Output_2(switch_6_output_2), .Output_3(switch_6_output_3),
    .Output_4(switch_6_output_4), .Output_5(switch_6_output_5), .Output_6(switch_6_output_6),
    .Output_7(switch_6_output_7), .Output_8(switch_6_output_8), .Output_9(switch_6_output_9), .ctrl(bus_0_2),
    .Let(rom_1_data));
  DotMatrix #(.matrixcols(9), .matrixrows(9)) dotmatrix_8 (
    .col0(switch_8_output), .col1(switch_8_output_2), .col2(switch_8_output_3), .col3(switch_8_output_4),
    .col4(switch_8_output_5), .col5(switch_8_output_6), .col6(switch_8_output_7), .col7(switch_8_output_8),
    .col8(switch_8_output_9));
  Switch switch_7 (
    .Output(switch_7_output), .Output_2(switch_7_output_2), .Output_3(switch_7_output_3),
    .Output_4(switch_7_output_4), .Output_5(switch_7_output_5), .Output_6(switch_7_output_6),
    .Output_7(switch_7_output_7), .Output_8(switch_7_output_8), .Output_9(switch_7_output_9), .ctrl(bus_0_2),
    .Let(rom_1_data));
  Switch switch_8 (
    .Output(switch_8_output), .Output_2(switch_8_output_2), .Output_3(switch_8_output_3),
    .Output_4(switch_8_output_4), .Output_5(switch_8_output_5), .Output_6(switch_8_output_6),
    .Output_7(switch_8_output_7), .Output_8(switch_8_output_8), .Output_9(switch_8_output_9), .ctrl(bus_0_2),
    .Let(rom_1_data));

  // Notes on the sheet:
  //   00) ABSOLUTE; CALENDAR
  //   10) ELEPHANT; MOUNTAIN
  //   20) PARADISE; ULTIMATE 
  //   30) WATERFAL; XENOPHOB
  //   40) COMPUTER; ENGINEER
  //   50) FESTIVAL; DISCOVER
  //   60) NAVIGATE; OPERATOR
  //   70) GENERATE; BEAUTIFY
  //   80) BUILDING; CHILDREN
  //   90) HOSPITAL; KITCHEN
  //   a0) LANGUAGE; MISTAKES
  //   b0) NOTEBOOK; PAINTING
  //   c0) QUESTION; RECEARCH
  //   d0)SOFTWARE; STRATEGY
  //   e0)TRAINING; VACATION
  //   contents of rom_1 (hex, n*v repeats v):
  //   1 2 13 f c 15 14 5 3 1 c 5 e 4 1 12 5 c 5 10 8 1 e 14 d f 15 e 14 1 9 e 10 1 12 1 4 9 13 5 15 c 14 9
  //   d 1 14 5 17 1 14 5 12 6 1 c 18 5 e f 10 8 f 2 3 f d 10 15 14 5 12 5 e 7 9 e 5 5 12 6 5 13 14 9 16 1
  //   c 4 9 13 3 f 16 5 12 e 1 16 9 7 1 14 5 f 10 5 12 1 14 f 12 7 5 e 5 12 1 14 5 2 5 1 15 14 9 6 19 2 15
  //   9 c 4 9 e 7 3 8 9 c 4 12 5 e 8 f 13 10 9 14 1 c b 9 14 3 8 5 e 13 c 1 e 7 15 1 7 5 d 9 13 14 1 b 5
  //   13 e f 14 5 2 f f b 10 1 e 14 9 e 7 7 11 15 5 13 14 9 f e 12 5 13 5 1 12 3 8 13 f 6 14 17 1 12 5 13
  //   14 12 1 14 5 7 19 14 12 1 9 e 9 e 7 16 1 3 1 14 9 f e
endmodule

module Switch (
  input  [4:0] Let,
  input  ctrl,
  output [8:0] Output,
  output [8:0] Output_2,
  output [8:0] Output_3,
  output [8:0] Output_4,
  output [8:0] Output_5,
  output [8:0] Output_6,
  output [8:0] Output_7,
  output [8:0] Output_8,
  output [8:0] Output_9
);

  wire [8:0] multiplexer_1_out, multiplexer_1_out_2, multiplexer_1_out_3, multiplexer_2_out,
       multiplexer_2_out_2, multiplexer_2_out_3, multiplexer_3_out, multiplexer_3_out_2, multiplexer_3_out_3;

  Transistor #(.\type ("n"), .width(9)) transistor_1 (.in(multiplexer_1_out_3), .out(Output), .gate(ctrl));
  Transistor #(.\type ("n"), .width(9)) transistor_2 (.in(multiplexer_1_out_2), .out(Output_2), .gate(ctrl));
  Multiplexer #(.select(5), .width(27), .enable("false")) multiplexer_1 (
    .in0({27{1'b0}}), .in1(27'h47e), .in2(27'h104fe), .in3(27'hf8fe), .in4(27'h104fe), .in5(27'h104fe),
    .in6(27'h104fe), .in7(27'hf8fe), .in8(27'h104fe), .in9(27'h18c82), .in10(27'h100e), .in11(27'h104fe),
    .in12(27'h104fe), .in13(27'h1fcfe), .in14(27'h1fcfe), .in15(27'hf8fe), .in16(27'h104fe), .in17(27'hf8fe),
    .in18(27'h1fcfe), .in19(27'hc8f4), .in20(27'h18082), .in21(27'h100fc), .in22(27'h1c018),
    .in23(27'h1f00e), .in24(27'h104c6), .in25(27'h100e0), .in26(27'h1c486), .in27({27{1'b0}}),
    .in28({27{1'b0}}), .in29({27{1'b0}}), .in30({27{1'b0}}), .in31({27{1'b0}}),
    .out({multiplexer_1_out_3, multiplexer_1_out_2, multiplexer_1_out}), .sel(Let));
  Transistor #(.\type ("n"), .width(9)) transistor_3 (.in(multiplexer_1_out), .out(Output_3), .gate(ctrl));
  Transistor #(.\type ("n"), .width(9)) transistor_4 (.in(multiplexer_2_out_3), .out(Output_4), .gate(ctrl));
  Transistor #(.\type ("n"), .width(9)) transistor_5 (.in(multiplexer_2_out_2), .out(Output_5), .gate(ctrl));
  Multiplexer #(.select(5), .width(27), .enable("false")) multiplexer_2 (
    .in0({27{1'b0}}), .in1(27'h24124fe), .in2(27'h3f92492), .in3(27'h2090482), .in4(27'h3f90482),
    .in5(27'h3f92492), .in6(27'h3f92490), .in7(27'h209249e), .in8(27'h24820fe), .in9(27'h3f9fc82),
    .in10(27'h30904fe), .in11(27'h3f92430), .in12(27'h3f80402), .in13(27'h882060), .in14(27'h180200c),
    .in15(27'h2090482), .in16(27'h3f91488), .in17(27'h2091086), .in18(27'h2493098), .in19(27'h2492492),
    .in20(27'h3f9fc82), .in21(27'h190cfe), .in22(27'h193cf8), .in23(27'hc0f00c), .in24(27'ha020ee),
    .in25(27'h893cfe), .in26(27'h23924e2), .in27({27{1'b0}}), .in28({27{1'b0}}), .in29({27{1'b0}}),
    .in30({27{1'b0}}), .in31({27{1'b0}}),
    .out({multiplexer_2_out_3, multiplexer_2_out_2, multiplexer_2_out}), .sel(Let));
  Transistor #(.\type ("n"), .width(9)) transistor_6 (.in(multiplexer_2_out), .out(Output_6), .gate(ctrl));
  Transistor #(.\type ("n"), .width(9)) transistor_7 (.in(multiplexer_3_out_3), .out(Output_7), .gate(ctrl));
  Transistor #(.\type ("n"), .width(9)) transistor_8 (.in(multiplexer_3_out_2), .out(Output_8), .gate(ctrl));
  Multiplexer #(.select(5), .width(27), .enable("false")) multiplexer_3 (
    .in0({27{1'b0}}), .in1(27'h1f80400), .in2(27'h3f8d800), .in3(27'h318c800), .in4(27'h3f8f800),
    .in5(27'h2098c00), .in6(27'h2018000), .in7(27'h378a000), .in8(27'h3f90400), .in9(27'h3198c00),
    .in10(27'h3f10000), .in11(27'h3790400), .in12(27'h81c00), .in13(27'h3f9fc00), .in14(27'h3f9fc00),
    .in15(27'h3f8f800), .in16(27'h3e0e000), .in17(27'h3f8f400), .in18(27'h3d8c400), .in19(27'h3789800),
    .in20(27'h3018000), .in21(27'h3f10000), .in22(27'h3810000), .in23(27'h3f9f000), .in24(27'h3190400),
    .in25(27'h3890000), .in26(27'h3091c00), .in27({27{1'b0}}), .in28({27{1'b0}}), .in29({27{1'b0}}),
    .in30({27{1'b0}}), .in31({27{1'b0}}),
    .out({multiplexer_3_out_3, multiplexer_3_out_2, multiplexer_3_out}), .sel(Let));
  Transistor #(.\type ("n"), .width(9)) transistor_9 (.in(multiplexer_3_out), .out(Output_9), .gate(ctrl));
  Transistor #(.gate("br"), .width(9)) transistor_10 (.in({9{1'b0}}), .out(Output), .gate(ctrl));
  Transistor #(.gate("br"), .width(9)) transistor_11 (.in(9'h7f), .out(Output_2), .gate(ctrl));
  Transistor #(.gate("br"), .width(9)) transistor_12 (.in(9'h80), .out(Output_3), .gate(ctrl));
  Transistor #(.gate("br"), .width(9)) transistor_13 (.in(9'h108), .out(Output_4), .gate(ctrl));
  Transistor #(.gate("br"), .width(9)) transistor_14 (.in(9'h100), .out(Output_5), .gate(ctrl));
  Transistor #(.gate("br"), .width(9)) transistor_15 (.in(9'h100), .out(Output_6), .gate(ctrl));
  Transistor #(.gate("br"), .width(9)) transistor_16 (.in(9'h80), .out(Output_7), .gate(ctrl));
  Transistor #(.gate("br"), .width(9)) transistor_17 (.in(9'h7f), .out(Output_8), .gate(ctrl));
  Transistor #(.gate("br"), .width(9)) transistor_18 (.in({9{1'b0}}), .out(Output_9), .gate(ctrl));
endmodule

module Alphabet (
);

  DotMatrix #(.matrixcols(9), .matrixrows(9)) dotmatrix_1 (
    .col0({9{1'b0}}), .col1(9'h2), .col2(9'h7e), .col3(9'h90), .col4(9'h92), .col5(9'hfe), .col6(9'h7e),
    .col7(9'h2), .col8({9{1'b0}}));
  DotMatrix #(.matrixcols(9), .matrixrows(9)) dotmatrix_2 (
    .col0({9{1'b0}}), .col1(9'h8), .col2(9'he), .col3(9'hc2), .col4(9'h82), .col5(9'hfe), .col6(9'hfc),
    .col7(9'h80), .col8({9{1'b0}}));
  DotMatrix #(.matrixcols(9), .matrixrows(9)) dotmatrix_3 (
    .col0({9{1'b0}}), .col1(9'h64), .col2(9'hf4), .col3(9'h92), .col4(9'h92), .col5(9'h92), .col6(9'hde),
    .col7(9'h4c), .col8({9{1'b0}}));
  DotMatrix #(.matrixcols(9), .matrixrows(9)) dotmatrix_4 (
    .col0({9{1'b0}}), .col1(9'h82), .col2(9'hfe), .col3(9'hfe), .col4(9'h92), .col5(9'h92), .col6(9'hfe),
    .col7(9'h6c), .col8({9{1'b0}}));
  DotMatrix #(.matrixcols(9), .matrixrows(9)) dotmatrix_5 (
    .col0({9{1'b0}}), .col1(9'h82), .col2(9'hfe), .col3(9'hfe), .col4(9'h92), .col5(9'h30), .col6(9'hde),
    .col7(9'h82), .col8({9{1'b0}}));
  DotMatrix #(.matrixcols(9), .matrixrows(9)) dotmatrix_6 (
    .col0({9{1'b0}}), .col1(9'hc0), .col2(9'h82), .col3(9'hfe), .col4(9'hfe), .col5(9'h82), .col6(9'hc0),
    .col7(9'hc0), .col8({9{1'b0}}));
  DotMatrix #(.matrixcols(9), .matrixrows(9)) dotmatrix_7 (
    .col0({9{1'b0}}), .col1(9'h7c), .col2(9'hfe), .col3(9'h82), .col4(9'h82), .col5(9'h82), .col6(9'hc6),
    .col7(9'h64), .col8({9{1'b0}}));
  DotMatrix #(.matrixcols(9), .matrixrows(9)) dotmatrix_8 (
    .col0({9{1'b0}}), .col1(9'h82), .col2(9'hfe), .col3(9'hfe), .col4(9'h2), .col5(9'h2), .col6(9'h2),
    .col7(9'he), .col8({9{1'b0}}));
  DotMatrix #(.matrixcols(9), .matrixrows(9)) dotmatrix_9 (
    .col0({9{1'b0}}), .col1(9'h80), .col2(9'hfc), .col3(9'h6), .col4(9'h86), .col5(9'hfe), .col6(9'hfc),
    .col7(9'h80), .col8({9{1'b0}}));
  DotMatrix #(.matrixcols(9), .matrixrows(9)) dotmatrix_10 (
    .col0({9{1'b0}}), .col1(9'h82), .col2(9'hfe), .col3(9'hfe), .col4(9'h82), .col5(9'h82), .col6(9'hfe),
    .col7(9'h7c), .col8({9{1'b0}}));
  DotMatrix #(.matrixcols(9), .matrixrows(9)) dotmatrix_11 (
    .col0({9{1'b0}}), .col1(9'hfe), .col2(9'hfe), .col3(9'h22), .col4(9'h10), .col5(9'h60), .col6(9'hfe),
    .col7(9'hfe), .col8({9{1'b0}}));
  DotMatrix #(.matrixcols(9), .matrixrows(9)) dotmatrix_12 (
    .col0({9{1'b0}}), .col1(9'he0), .col2(9'h18), .col3(9'h6), .col4(9'h9e), .col5(9'hf8), .col6(9'he0),
    .col7(9'h80), .col8({9{1'b0}}));
  DotMatrix #(.matrixcols(9), .matrixrows(9)) dotmatrix_13 (
    .col0({9{1'b0}}), .col1(9'h82), .col2(9'hfe), .col3(9'hfe), .col4(9'h92), .col5(9'h92), .col6(9'h82),
    .col7(9'hc6), .col8({9{1'b0}}));
  DotMatrix #(.matrixcols(9), .matrixrows(9)) dotmatrix_14 (
    .col0({9{1'b0}}), .col1(9'hfe), .col2(9'hfe), .col3(9'h60), .col4(9'h10), .col5(9'hc), .col6(9'hfe),
    .col7(9'hfe), .col8({9{1'b0}}));
  DotMatrix #(.matrixcols(9), .matrixrows(9)) dotmatrix_15 (
    .col0({9{1'b0}}), .col1(9'hf8), .col2(9'he), .col3(9'h30), .col4(9'h78), .col5(9'hc), .col6(9'hfe),
    .col7(9'hf8), .col8({9{1'b0}}));
  DotMatrix #(.matrixcols(9), .matrixrows(9)) dotmatrix_16 (
    .col0({9{1'b0}}), .col1(9'h82), .col2(9'hfe), .col3(9'hfe), .col4(9'h92), .col5(9'h90), .col6(9'h80),
    .col7(9'hc0), .col8({9{1'b0}}));
  DotMatrix #(.matrixcols(9), .matrixrows(9)) dotmatrix_17 (
    .col0({9{1'b0}}), .col1(9'h7c), .col2(9'hfe), .col3(9'h82), .col4(9'h82), .col5(9'h82), .col6(9'hfe),
    .col7(9'h7c), .col8({9{1'b0}}));
  DotMatrix #(.matrixcols(9), .matrixrows(9)) dotmatrix_18 (
    .col0({9{1'b0}}), .col1(9'h82), .col2(9'hc6), .col3(9'h28), .col4(9'h10), .col5(9'hee), .col6(9'hc6),
    .col7(9'h82), .col8({9{1'b0}}));
  DotMatrix #(.matrixcols(9), .matrixrows(9)) dotmatrix_19 (
    .col0({9{1'b0}}), .col1(9'h7c), .col2(9'hfe), .col3(9'h82), .col4(9'h92), .col5(9'h9e), .col6(9'hde),
    .col7(9'h50), .col8({9{1'b0}}));
  DotMatrix #(.matrixcols(9), .matrixrows(9)) dotmatrix_20 (
    .col0({9{1'b0}}), .col1(9'h82), .col2(9'hfe), .col3(9'hfe), .col4(9'h8a), .col5(9'h88), .col6(9'hf8),
    .col7(9'h70), .col8({9{1'b0}}));
  DotMatrix #(.matrixcols(9), .matrixrows(9)) dotmatrix_21 (
    .col0({9{1'b0}}), .col1(9'h80), .col2(9'he0), .col3(9'h22), .col4(9'h9e), .col5(9'hfe), .col6(9'he2),
    .col7(9'h80), .col8({9{1'b0}}));
  DotMatrix #(.matrixcols(9), .matrixrows(9)) dotmatrix_22 (
    .col0({9{1'b0}}), .col1(9'h82), .col2(9'hfe), .col3(9'h92), .col4(9'h10), .col5(9'hfe), .col6(9'hfe),
    .col7(9'h82), .col8({9{1'b0}}));
  DotMatrix #(.matrixcols(9), .matrixrows(9)) dotmatrix_23 (
    .col0({9{1'b0}}), .col1(9'h7c), .col2(9'hfe), .col3(9'h82), .col4(9'h88), .col5(9'h86), .col6(9'hfe),
    .col7(9'h7a), .col8({9{1'b0}}));
  DotMatrix #(.matrixcols(9), .matrixrows(9)) dotmatrix_24 (
    .col0({9{1'b0}}), .col1(9'he2), .col2(9'h86), .col3(9'h8e), .col4(9'h92), .col5(9'he2), .col6(9'hc2),
    .col7(9'h8e), .col8({9{1'b0}}));
  DotMatrix #(.matrixcols(9), .matrixrows(9)) dotmatrix_25 (
    .col0({9{1'b0}}), .col1(9'hc6), .col2(9'h82), .col3(9'hfe), .col4(9'hfe), .col5(9'h82), .col6(9'hc6),
    .col7(9'hc6), .col8({9{1'b0}}));
  DotMatrix #(.matrixcols(9), .matrixrows(9)) dotmatrix_26 (
    .col0({9{1'b0}}), .col1(9'hfe), .col2(9'hfe), .col3(9'h92), .col4(9'h98), .col5(9'h98), .col6(9'hf6),
    .col7(9'h62), .col8({9{1'b0}}));
  DotMatrix #(.matrixcols(9), .matrixrows(9)) dotmatrix_27 (
    .col0({9{1'b0}}), .col1(9'h7f), .col2(9'h80), .col3(9'h108), .col4(9'h100), .col5(9'h100), .col6(9'h80),
    .col7(9'h7f), .col8({9{1'b0}}));
endmodule

module CDM_test (
  input  [4:0] bus_0,
  input  bus_0_2,
  input  bus_0_3
);

  wire A_out, B_out, bt, button_1_out, C_out, cdm_8_2_p3, cdm_8_2_p4, cl, code, D_out, data, E_out, F_out,
       G_out, H_out, I_out, J_out, K_out, L_out, M_out, N_out, not_1_out, O_out, P_out, Q_out, R_out, rd_wr,
       S_out, T_out, U_out, V_out, W_out, X_out, Y_out, Z_out;
  wire [4:0] random_1_out, register_1_q, rom_1_data, transistor_1_out;
  wire [7:0] cdm_8_2_p6, cdm_8_2_p7, cdm_8_2_p8, controlled_buffer_27_out;
  wire [8:0] switch_1_output, switch_1_output_2, switch_1_output_3, switch_1_output_4, switch_1_output_5,
       switch_1_output_6, switch_1_output_7, switch_1_output_8, switch_1_output_9, switch_2_output,
       switch_2_output_2, switch_2_output_3, switch_2_output_4, switch_2_output_5, switch_2_output_6,
       switch_2_output_7, switch_2_output_8, switch_2_output_9, switch_3_output, switch_3_output_2,
       switch_3_output_3, switch_3_output_4, switch_3_output_5, switch_3_output_6, switch_3_output_7,
       switch_3_output_8, switch_3_output_9, switch_4_output, switch_4_output_2, switch_4_output_3,
       switch_4_output_4, switch_4_output_5, switch_4_output_6, switch_4_output_7, switch_4_output_8,
       switch_4_output_9, switch_5_output, switch_5_output_2, switch_5_output_3, switch_5_output_4,
       switch_5_output_5, switch_5_output_6, switch_5_output_7, switch_5_output_8, switch_5_output_9,
       switch_6_output, switch_6_output_2, switch_6_output_3, switch_6_output_4, switch_6_output_5,
       switch_6_output_6, switch_6_output_7, switch_6_output_8, switch_6_output_9, switch_7_output,
       switch_7_output_2, switch_7_output_3, switch_7_output_4, switch_7_output_5, switch_7_output_6,
       switch_7_output_7, switch_7_output_8, switch_7_output_9, switch_8_output, switch_8_output_2,
       switch_8_output_3, switch_8_output_4, switch_8_output_5, switch_8_output_6, switch_8_output_7,
       switch_8_output_8, switch_8_output_9;

  Random #(.width(5)) random_1 (.clk(bus_0_3), .out(random_1_out));  // open: next, clr
  // Probe on rom_1_data
  // Probe on random_1_out
  Button A (.out(A_out));
  assign bt = A_out ? A_out : 1'bz;  // Controlled_Buffer controlled_buffer_1
  Button J (.out(J_out));
  assign bt = J_out ? J_out : 1'bz;  // Controlled_Buffer controlled_buffer_2
  Button S (.out(S_out));
  assign bt = S_out ? S_out : 1'bz;  // Controlled_Buffer controlled_buffer_3
  DotMatrix #(.matrixcols(9), .matrixrows(9)) dotmatrix_1 (
    .col0(switch_1_output), .col1(switch_1_output_2), .col2(switch_1_output_3), .col3(switch_1_output_4),
    .col4(switch_1_output_5), .col5(switch_1_output_6), .col6(switch_1_output_7), .col7(switch_1_output_8),
    .col8(switch_1_output_9));
  ROM #(.dataWidth(5)) rom_1 (.addr({random_1_out, 3'b000}), .data(rom_1_data));  // open: sel
  Pull_Resistor pull_resistor_1 (.node(bt));
  Transistor #(.\type ("n"), .width(5)) transistor_1 (.in(5'b00001), .out(transistor_1_out), .gate(A_out));
  Button B (.out(B_out));
  assign bt = B_out ? B_out : 1'bz;  // Controlled_Buffer controlled_buffer_4
  Transistor #(.\type ("n"), .width(5)) transistor_2 (.in(5'b01010), .out(transistor_1_out), .gate(J_out));
  Button K (.out(K_out));
  assign bt = K_out ? K_out : 1'bz;  // Controlled_Buffer controlled_buffer_5
  Transistor #(.\type ("n"), .width(5)) transistor_3 (.in(5'b10011), .out(transistor_1_out), .gate(S_out));
  Button T (.out(T_out));
  assign bt = T_out ? T_out : 1'bz;  // Controlled_Buffer controlled_buffer_6
  DotMatrix #(.matrixcols(9), .matrixrows(9)) dotmatrix_2 (
    .col0(switch_2_output), .col1(switch_2_output_2), .col2(switch_2_output_3), .col3(switch_2_output_4),
    .col4(switch_2_output_5), .col5(switch_2_output_6), .col6(switch_2_output_7), .col7(switch_2_output_8),
    .col8(switch_2_output_9));
  // CdM_8 cdm_8_1: pin names not known; wires that end beside it: bus_0
  Switch switch_1 (
    .Output(switch_1_output), .Output_2(switch_1_output_2), .Output_3(switch_1_output_3),
    .Output_4(switch_1_output_4), .Output_5(switch_1_output_5), .Output_6(switch_1_output_6),
    .Output_7(switch_1_output_7), .Output_8(switch_1_output_8), .Output_9(switch_1_output_9), .ctrl(bus_0_2),
    .Let(rom_1_data));
  Register #(.width(5)) register_1 (.D(transistor_1_out), .Q(register_1_q), .clk(bt));  // open: en, clr
  // Probe on register_1_q
  Transistor #(.\type ("n"), .width(5)) transistor_4 (.in(5'b00010), .out(transistor_1_out), .gate(B_out));
  Transistor #(.\type ("n"), .width(5)) transistor_5 (.in(5'b00011), .out(transistor_1_out), .gate(C_out));
  Button C (.out(C_out));
  assign bt = C_out ? C_out : 1'bz;  // Controlled_Buffer controlled_buffer_7
  Transistor #(.\type ("n"), .width(5)) transistor_6 (.in(5'b01011), .out(transistor_1_out), .gate(K_out));
  Transistor #(.\type ("n"), .width(5)) transistor_7 (.in(5'b01100), .out(transistor_1_out), .gate(L_out));
  Button L (.out(L_out));
  assign bt = L_out ? L_out : 1'bz;  // Controlled_Buffer controlled_buffer_8
  Transistor #(.\type ("n"), .width(5)) transistor_8 (.in(5'b10101), .out(transistor_1_out), .gate(U_out));
  Transistor #(.\type ("n"), .width(5)) transistor_9 (.in(5'b10100), .out(transistor_1_out), .gate(T_out));
  Button U (.out(U_out));
  assign bt = U_out ? U_out : 1'bz;  // Controlled_Buffer controlled_buffer_9
  Switch switch_2 (
    .Output(switch_2_output), .Output_2(switch_2_output_2), .Output_3(switch_2_output_3),
    .Output_4(switch_2_output_4), .Output_5(switch_2_output_5), .Output_6(switch_2_output_6),
    .Output_7(switch_2_output_7), .Output_8(switch_2_output_8), .Output_9(switch_2_output_9), .ctrl(bus_0_2),
    .Let(rom_1_data));
  Transistor #(.\type ("n"), .width(5)) transistor_10 (.in(5'b00100), .out(transistor_1_out), .gate(D_out));
  Button E (.out(E_out));
  Button D (.out(D_out));
  assign bt = D_out ? D_out : 1'bz;  // Controlled_Buffer controlled_buffer_10
  assign bt = E_out ? E_out : 1'bz;  // Controlled_Buffer controlled_buffer_11
  Transistor #(.\type ("n"), .width(5)) transistor_11 (.in(5'b01101), .out(transistor_1_out), .gate(M_out));
  Button N (.out(N_out));
  Button M (.out(M_out));
  assign bt = N_out ? N_out : 1'bz;  // Controlled_Buffer controlled_buffer_12
  assign bt = M_out ? M_out : 1'bz;  // Controlled_Buffer controlled_buffer_13
  Transistor #(.\type ("n"), .width(5)) transistor_12 (.in(5'b10110), .out(transistor_1_out), .gate(V_out));
  Button V (.out(V_out));
  Button W (.out(W_out));
  assign bt = V_out ? V_out : 1'bz;  // Controlled_Buffer controlled_buffer_14
  assign bt = W_out ? W_out : 1'bz;  // Controlled_Buffer controlled_buffer_15
  DotMatrix #(.matrixcols(9), .matrixrows(9)) dotmatrix_3 (
    .col0(switch_3_output), .col1(switch_3_output_2), .col2(switch_3_output_3), .col3(switch_3_output_4),
    .col4(switch_3_output_5), .col5(switch_3_output_6), .col6(switch_3_output_7), .col7(switch_3_output_8),
    .col8(switch_3_output_9));
  Clock clock_1 (.out(cl));
  Button button_1 (.out(button_1_out));
  Transistor #(.\type ("n"), .width(5)) transistor_13 (.in(5'b00101), .out(transistor_1_out), .gate(E_out));
  Button F (.out(F_out));
  assign bt = F_out ? F_out : 1'bz;  // Controlled_Buffer controlled_buffer_16
  Transistor #(.\type ("n"), .width(5)) transistor_14 (.in(5'b01110), .out(transistor_1_out), .gate(N_out));
  Button O (.out(O_out));
  assign bt = O_out ? O_out : 1'bz;  // Controlled_Buffer controlled_buffer_17
  Transistor #(.\type ("n"), .width(5)) transistor_15 (.in(5'b10111), .out(transistor_1_out), .gate(W_out));
  Button X (.out(X_out));
  assign bt = X_out ? X_out : 1'bz;  // Controlled_Buffer controlled_buffer_18
  DotMatrix #(.matrixcols(9), .matrixrows(9)) dotmatrix_4 (
    .col0(switch_4_output), .col1(switch_4_output_2), .col2(switch_4_output_3), .col3(switch_4_output_4),
    .col4(switch_4_output_5), .col5(switch_4_output_6), .col6(switch_4_output_7), .col7(switch_4_output_8),
    .col8(switch_4_output_9));
  Switch switch_3 (
    .Output(switch_3_output), .Output_2(switch_3_output_2), .Output_3(switch_3_output_3),
    .Output_4(switch_3_output_4), .Output_5(switch_3_output_5), .Output_6(switch_3_output_6),
    .Output_7(switch_3_output_7), .Output_8(switch_3_output_8), .Output_9(switch_3_output_9), .ctrl(bus_0_2),
    .Let(rom_1_data));
  Transistor #(.\type ("n"), .width(5)) transistor_16 (.in(5'b00111), .out(transistor_1_out), .gate(G_out));
  Transistor #(.\type ("n"), .width(5)) transistor_17 (.in(5'b00110), .out(transistor_1_out), .gate(F_out));
  Button G (.out(G_out));
  assign bt = G_out ? G_out : 1'bz;  // Controlled_Buffer controlled_buffer_19
  Transistor #(.\type ("n"), .width(5)) transistor_18 (.in(5'b01111), .out(transistor_1_out), .gate(O_out));
  Transistor #(.\type ("n"), .width(5)) transistor_19 (.in(5'b10000), .out(transistor_1_out), .gate(P_out));
  Button P (.out(P_out));
  assign bt = P_out ? P_out : 1'bz;  // Controlled_Buffer controlled_buffer_20
  Transistor #(.\type ("n"), .width(5)) transistor_20 (.in(5'b11000), .out(transistor_1_out), .gate(X_out));
  Transistor #(.\type ("n"), .width(5)) transistor_21 (.in(5'b11001), .out(transistor_1_out), .gate(Y_out));
  Button Y (.out(Y_out));
  assign bt = Y_out ? Y_out : 1'bz;  // Controlled_Buffer controlled_buffer_21
  DotMatrix #(.matrixcols(9), .matrixrows(9)) dotmatrix_5 (
    .col0(switch_5_output), .col1(switch_5_output_2), .col2(switch_5_output_3), .col3(switch_5_output_4),
    .col4(switch_5_output_5), .col5(switch_5_output_6), .col6(switch_5_output_7), .col7(switch_5_output_8),
    .col8(switch_5_output_9));
  Switch switch_4 (
    .Output(switch_4_output), .Output_2(switch_4_output_2), .Output_3(switch_4_output_3),
    .Output_4(switch_4_output_4), .Output_5(switch_4_output_5), .Output_6(switch_4_output_6),
    .Output_7(switch_4_output_7), .Output_8(switch_4_output_8), .Output_9(switch_4_output_9), .ctrl(bus_0_2),
    .Let(rom_1_data));
  // CdM_8 cdm_8_2: pin names not known; wires that end beside it: cl, button_1_out, cdm_8_2_p3, cdm_8_2_p4, rd_wr, cdm_8_2_p6, cdm_8_2_p7, cdm_8_2_p8
  Transistor #(.\type ("n"), .width(5)) transistor_22 (.in(5'b01000), .out(transistor_1_out), .gate(H_out));
  Button I (.out(I_out));
  Button H (.out(H_out));
  assign bt = I_out ? I_out : 1'bz;  // Controlled_Buffer controlled_buffer_22
  assign bt = H_out ? H_out : 1'bz;  // Controlled_Buffer controlled_buffer_23
  Transistor #(.\type ("n"), .width(5)) transistor_23 (.in(5'b10001), .out(transistor_1_out), .gate(Q_out));
  Button Q (.out(Q_out));
  Button R (.out(R_out));
  assign bt = R_out ? R_out : 1'bz;  // Controlled_Buffer controlled_buffer_24
  assign bt = Q_out ? Q_out : 1'bz;  // Controlled_Buffer controlled_buffer_25
  Transistor #(.\type ("n"), .width(5)) transistor_24 (.in(5'b11010), .out(transistor_1_out), .gate(Z_out));
  Button Z (.out(Z_out));
  assign bt = Z_out ? Z_out : 1'bz;  // Controlled_Buffer controlled_buffer_26
  DotMatrix #(.matrixcols(9), .matrixrows(9)) dotmatrix_6 (
    .col0(switch_6_output), .col1(switch_6_output_2), .col2(switch_6_output_3), .col3(switch_6_output_4),
    .col4(switch_6_output_5), .col5(switch_6_output_6), .col6(switch_6_output_7), .col7(switch_6_output_8),
    .col8(switch_6_output_9));
  Switch switch_5 (
    .Output(switch_5_output), .Output_2(switch_5_output_2), .Output_3(switch_5_output_3),
    .Output_4(switch_5_output_4), .Output_5(switch_5_output_5), .Output_6(switch_5_output_6),
    .Output_7(switch_5_output_7), .Output_8(switch_5_output_8), .Output_9(switch_5_output_9), .ctrl(bus_0_2),
    .Let(rom_1_data));
  Decoder decoder_1 (.out0(code), .out1(data), .sel(cdm_8_2_p3), .en(cdm_8_2_p4));
  assign controlled_buffer_27_out = not_1_out ? cdm_8_2_p7 : 8'bz;  // Controlled_Buffer controlled_buffer_27
  not not_1 (not_1_out, rd_wr);
  assign cdm_8_2_p8 = rd_wr ? controlled_buffer_27_out : 8'bz;  // Controlled_Buffer controlled_buffer_28
  Transistor #(.\type ("n"), .width(5)) transistor_25 (.in(5'b01001), .out(transistor_1_out), .gate(I_out));
  Transistor #(.\type ("n"), .width(5)) transistor_26 (.in(5'b10010), .out(transistor_1_out), .gate(R_out));
  Switch switch_6 (
    .Output(switch_6_output), .Output_2(switch_6_output_2), .Output_3(switch_6_output_3),
    .Output_4(switch_6_output_4), .Output_5(switch_6_output_5), .Output_6(switch_6_output_6),
    .Output_7(switch_6_output_7), .Output_8(switch_6_output_8), .Output_9(switch_6_output_9), .ctrl(bus_0_2),
    .Let(rom_1_data));
  DotMatrix #(.matrixcols(9), .matrixrows(9)) dotmatrix_7 (
    .col0(switch_7_output), .col1(switch_7_output_2), .col2(switch_7_output_3), .col3(switch_7_output_4),
    .col4(switch_7_output_5), .col5(switch_7_output_6), .col6(switch_7_output_7), .col7(switch_7_output_8),
    .col8(switch_7_output_9));
  DotMatrix #(.matrixcols(9), .matrixrows(9)) dotmatrix_8 (
    .col0(switch_8_output), .col1(switch_8_output_2), .col2(switch_8_output_3), .col3(switch_8_output_4),
    .col4(switch_8_output_5), .col5(switch_8_output_6), .col6(switch_8_output_7), .col7(switch_8_output_8),
    .col8(switch_8_output_9));
  Switch switch_7 (
    .Output(switch_7_output), .Output_2(switch_7_output_2), .Output_3(switch_7_output_3),
    .Output_4(switch_7_output_4), .Output_5(switch_7_output_5), .Output_6(switch_7_output_6),
    .Output_7(switch_7_output_7), .Output_8(switch_7_output_8), .Output_9(switch_7_output_9), .ctrl(bus_0_2),
    .Let(rom_1_data));
  ROM rom_2 (.addr(cdm_8_2_p6), .data(controlled_buffer_27_out), .sel(code));
  RAM ram_1 (.addr(cdm_8_2_p6), .data(controlled_buffer_27_out), .sel(data), .clk(cl), .ld(rd_wr));  // open: clr
  Switch switch_8 (
    .Output(switch_8_output), .Output_2(switch_8_output_2), .Output_3(switch_8_output_3),
    .Output_4(switch_8_output_4), .Output_5(switch_8_output_5), .Output_6(switch_8_output_6),
    .Output_7(switch_8_output_7), .Output_8(switch_8_output_8), .Output_9(switch_8_output_9), .ctrl(bus_0_2),
    .Let(rom_1_data));

  // Notes on the sheet:
  //   contents of rom_1 (hex, n*v repeats v):
  //   1 2 13 f c 15 14 5 3 1 c 5 e 4 1 12 5 c 5 10 8 1 e 14 d f 15 e 14 1 9 e 10 1 12 1 4 9 13 5 15 c 14 9
  //   d 1 14 5 17 1 14 5 12 6 1 c 18 5 e f 10 8 f 2 3 f d 10 15 14 5 12 5 e 7 9 e 5 5 12 6 5 13 14 9 16 1
  //   c 4 9 13 3 f 16 5 12 e 1 16 9 7 1 14 5 f 10 5 12 1 14 f 12 7 5 e 5 12 1 14 5 2 5 1 15 14 9 6 19 2 15
  //   9 c 4 9 e 7 3 8 9 c 4 12 5 e 8 f 13 10 9 14 1 c b 9 14 3 8 5 e 13 c 1 e 7 15 1 7 5 d 9 13 14 1 b 5
  //   13 e f 14 5 2 f f b 10 1 e 14 9 e 7 7 11 15 5 13 14 9 f e 12 5 13 5 1 12 3 8 13 f 6 14 17 1 12 5 13
  //   14 12 1 14 5 7 19 14 12 1 9 e 9 e 7 16 1 3 1 14 9 f e
endmodule
