// Logisim project CSProject 6.8.circ as structural Verilog: 16 circuits, main circuit main
module main (
);

  wire btA, btB, btC, btD, btE, btF, btG, btH, btI, btJ, btK, btL, btM, btN, btO, btP, btQ, btR, btS, btT,
       btU, btV, btW, btX, btY, btZ, enter, halt, reset;
  wire [3:0] backend_1_display, counter_invertor_1_output;
  wire [4:0] \let ;
  wire [7:0] result;
  wire [8:0] animation_controller_1_matrix1, animation_controller_1_matrix1_2,
       animation_controller_1_matrix1_3, animation_controller_1_matrix1_4, animation_controller_1_matrix1_5,
       animation_controller_1_matrix1_6, animation_controller_1_matrix1_7, animation_controller_1_matrix1_8,
       animation_controller_1_matrix1_9, animation_controller_1_matrix2, animation_controller_1_matrix2_2,
       animation_controller_1_matrix2_3, animation_controller_1_matrix2_4, animation_controller_1_matrix2_5,
       animation_controller_1_matrix2_6, animation_controller_1_matrix2_7, animation_controller_1_matrix2_8,
       animation_controller_1_matrix2_9, animation_controller_1_matrix3, animation_controller_1_matrix3_2,
       animation_controller_1_matrix3_3, animation_controller_1_matrix3_4, animation_controller_1_matrix3_5,
       animation_controller_1_matrix3_6, animation_controller_1_matrix3_7, animation_controller_1_matrix3_8,
       animation_controller_1_matrix3_9, animation_controller_1_matrix4, animation_controller_1_matrix4_2,
       animation_controller_1_matrix4_3, animation_controller_1_matrix4_4, animation_controller_1_matrix4_5,
       animation_controller_1_matrix4_6, animation_controller_1_matrix4_7, animation_controller_1_matrix4_8,
       animation_controller_1_matrix4_9, animation_controller_1_matrix5, animation_controller_1_matrix5_2,
       animation_controller_1_matrix5_3, animation_controller_1_matrix5_4, animation_controller_1_matrix5_5,
       animation_controller_1_matrix5_6, animation_controller_1_matrix5_7, animation_controller_1_matrix5_8,
       animation_controller_1_matrix5_9, animation_controller_1_matrix6, animation_controller_1_matrix6_2,
       animation_controller_1_matrix6_3, animation_controller_1_matrix6_4, animation_controller_1_matrix6_5,
       animation_controller_1_matrix6_6, animation_controller_1_matrix6_7, animation_controller_1_matrix6_8,
       animation_controller_1_matrix6_9, animation_controller_1_matrix7, animation_controller_1_matrix7_2,
       animation_controller_1_matrix7_3, animation_controller_1_matrix7_4, animation_controller_1_matrix7_5,
       animation_controller_1_matrix7_6, animation_controller_1_matrix7_7, animation_controller_1_matrix7_8,
       animation_controller_1_matrix7_9, animation_controller_1_matrix8, animation_controller_1_matrix8_2,
       animation_controller_1_matrix8_3, animation_controller_1_matrix8_4, animation_controller_1_matrix8_5,
       animation_controller_1_matrix8_6, animation_controller_1_matrix8_7, animation_controller_1_matrix8_8,
       animation_controller_1_matrix8_9, animation_controller_1_matrix9, animation_controller_1_matrix9_2,
       animation_controller_1_matrix9_3, animation_controller_1_matrix9_4, animation_controller_1_matrix9_5,
       animation_controller_1_matrix9_6, animation_controller_1_matrix9_7, animation_controller_1_matrix9_8,
       animation_controller_1_matrix9_9, animation_controller_1_matrix10, animation_controller_1_matrix10_2,
       animation_controller_1_matrix10_3, animation_controller_1_matrix10_4,
       animation_controller_1_matrix10_5, animation_controller_1_matrix10_6,
       animation_controller_1_matrix10_7, animation_controller_1_matrix10_8,
       animation_controller_1_matrix10_9, backend_1_matrix1, backend_1_matrix1_2, backend_1_matrix1_3,
       backend_1_matrix1_4, backend_1_matrix1_5, backend_1_matrix1_6, backend_1_matrix1_7,
       backend_1_matrix1_8, backend_1_matrix1_9, backend_1_matrix2, backend_1_matrix2_2, backend_1_matrix2_3,
       backend_1_matrix2_4, backend_1_matrix2_5, backend_1_matrix2_6, backend_1_matrix2_7,
       backend_1_matrix2_8, backend_1_matrix2_9, backend_1_matrix3, backend_1_matrix3_2, backend_1_matrix3_3,
       backend_1_matrix3_4, backend_1_matrix3_5, backend_1_matrix3_6, backend_1_matrix3_7,
       backend_1_matrix3_8, backend_1_matrix3_9, backend_1_matrix4, backend_1_matrix4_2, backend_1_matrix4_3,
       backend_1_matrix4_4, backend_1_matrix4_5, backend_1_matrix4_6, backend_1_matrix4_7,
       backend_1_matrix4_8, backend_1_matrix4_9, backend_1_matrix5, backend_1_matrix5_2, backend_1_matrix5_3,
       backend_1_matrix5_4, backend_1_matrix5_5, backend_1_matrix5_6, backend_1_matrix5_7,
       backend_1_matrix5_8, backend_1_matrix5_9, backend_1_matrix6, backend_1_matrix6_2, backend_1_matrix6_3,
       backend_1_matrix6_4, backend_1_matrix6_5, backend_1_matrix6_6, backend_1_matrix6_7,
       backend_1_matrix6_8, backend_1_matrix6_9, backend_1_matrix7, backend_1_matrix7_2, backend_1_matrix7_3,
       backend_1_matrix7_4, backend_1_matrix7_5, backend_1_matrix7_6, backend_1_matrix7_7,
       backend_1_matrix7_8, backend_1_matrix7_9, backend_1_matrix8, backend_1_matrix8_2, backend_1_matrix8_3,
       backend_1_matrix8_4, backend_1_matrix8_5, backend_1_matrix8_6, backend_1_matrix8_7,
       backend_1_matrix8_8, backend_1_matrix8_9, basic_switch_1_output, basic_switch_1_output_2,
       basic_switch_1_output_3, basic_switch_1_output_4, basic_switch_1_output_5, basic_switch_1_output_6,
       basic_switch_1_output_7, basic_switch_1_output_8, basic_switch_1_output_9;

  DotMatrix #(.matrixcols(9), .matrixrows(9)) dotmatrix_1 (
    .col0(animation_controller_1_matrix1_9), .col1(animation_controller_1_matrix1_8),
    .col2(animation_controller_1_matrix1_7), .col3(animation_controller_1_matrix1_6),
    .col4(animation_controller_1_matrix1_5), .col5(animation_controller_1_matrix1_4),
    .col6(animation_controller_1_matrix1_3), .col7(animation_controller_1_matrix1_2),
    .col8(animation_controller_1_matrix1));
  DotMatrix #(.matrixcols(9), .matrixrows(9)) dotmatrix_2 (
    .col0(animation_controller_1_matrix2), .col1(animation_controller_1_matrix2_2),
    .col2(animation_controller_1_matrix2_3), .col3(animation_controller_1_matrix2_4),
    .col4(animation_controller_1_matrix2_5), .col5(animation_controller_1_matrix2_6),
    .col6(animation_controller_1_matrix2_7), .col7(animation_controller_1_matrix2_8),
    .col8(animation_controller_1_matrix2_9));
  counter_invertor counter_invertor_1 (.\output (counter_invertor_1_output), .\input (backend_1_display));
  Hex_Digit_Display hex_digit_display_1 (.value(counter_invertor_1_output));  // open: dp
  DotMatrix #(.matrixcols(9), .matrixrows(9)) dotmatrix_3 (
    .col0(backend_1_matrix1_9), .col1(backend_1_matrix1_8), .col2(backend_1_matrix1_7),
    .col3(backend_1_matrix1_6), .col4(backend_1_matrix1_5), .col5(backend_1_matrix1_4),
    .col6(backend_1_matrix1_3), .col7(backend_1_matrix1_2), .col8(backend_1_matrix1));
  DotMatrix #(.matrixcols(9), .matrixrows(9)) dotmatrix_4 (
    .col0(animation_controller_1_matrix3_9), .col1(animation_controller_1_matrix3_8),
    .col2(animation_controller_1_matrix3_7), .col3(animation_controller_1_matrix3_6),
    .col4(animation_controller_1_matrix3_5), .col5(animation_controller_1_matrix3_4),
    .col6(animation_controller_1_matrix3_3), .col7(animation_controller_1_matrix3_2),
    .col8(animation_controller_1_matrix3));
  DotMatrix #(.matrixcols(9), .matrixrows(9)) dotmatrix_5 (
    .col0(backend_1_matrix2), .col1(backend_1_matrix2_2), .col2(backend_1_matrix2_3),
    .col3(backend_1_matrix2_4), .col4(backend_1_matrix2_5), .col5(backend_1_matrix2_6),
    .col6(backend_1_matrix2_7), .col7(backend_1_matrix2_8), .col8(backend_1_matrix2_9));
  DotMatrix #(.matrixcols(9), .matrixrows(9)) dotmatrix_6 (
    .col0(animation_controller_1_matrix4), .col1(animation_controller_1_matrix4_2),
    .col2(animation_controller_1_matrix4_3), .col3(animation_controller_1_matrix4_4),
    .col4(animation_controller_1_matrix4_5), .col5(animation_controller_1_matrix4_6),
    .col6(animation_controller_1_matrix4_7), .col7(animation_controller_1_matrix4_8),
    .col8(animation_controller_1_matrix4_9));
  DotMatrix #(.matrixcols(9), .matrixrows(9)) dotmatrix_7 (
    .col0(backend_1_matrix3_9), .col1(backend_1_matrix3_8), .col2(backend_1_matrix3_7),
    .col3(backend_1_matrix3_6), .col4(backend_1_matrix3_5), .col5(backend_1_matrix3_4),
    .col6(backend_1_matrix3_3), .col7(backend_1_matrix3_2), .col8(backend_1_matrix3));
  Button New_Game (.out(reset));
  Button W (.out(btW));
  Button Q (.out(btQ));
  Button E (.out(btE));
  Button A (.out(btA));
  Button S (.out(btS));
  Button D (.out(btD));
  Button X (.out(btX));
  Button Z (.out(btZ));
  DotMatrix #(.matrixcols(9), .matrixrows(9)) dotmatrix_8 (
    .col0(animation_controller_1_matrix5_9), .col1(animation_controller_1_matrix5_8),
    .col2(animation_controller_1_matrix5_7), .col3(animation_controller_1_matrix5_6),
    .col4(animation_controller_1_matrix5_5), .col5(animation_controller_1_matrix5_4),
    .col6(animation_controller_1_matrix5_3), .col7(animation_controller_1_matrix5_2),
    .col8(animation_controller_1_matrix5));
  Animation_Controller animation_controller_1 (
    .matrix1(animation_controller_1_matrix1), .matrix3(animation_controller_1_matrix3),
    .matrix5(animation_controller_1_matrix5), .matrix7(animation_controller_1_matrix7),
    .matrix9(animation_controller_1_matrix9), .matrix1_2(animation_controller_1_matrix1_2),
    .matrix3_2(animation_controller_1_matrix3_2), .matrix5_2(animation_controller_1_matrix5_2),
    .matrix7_2(animation_controller_1_matrix7_2), .matrix9_2(animation_controller_1_matrix9_2),
    .matrix1_3(animation_controller_1_matrix1_3), .matrix3_3(animation_controller_1_matrix3_3),
    .matrix5_3(animation_controller_1_matrix5_3), .matrix7_3(animation_controller_1_matrix7_3),
    .matrix9_3(animation_controller_1_matrix9_3), .matrix1_4(animation_controller_1_matrix1_4),
    .matrix3_4(animation_controller_1_matrix3_4), .matrix5_4(animation_controller_1_matrix5_4),
    .matrix7_4(animation_controller_1_matrix7_4), .matrix9_4(animation_controller_1_matrix9_4),
    .matrix1_5(animation_controller_1_matrix1_5), .matrix3_5(animation_controller_1_matrix3_5),
    .matrix5_5(animation_controller_1_matrix5_5), .matrix7_5(animation_controller_1_matrix7_5),
    .matrix9_5(animation_controller_1_matrix9_5), .matrix1_6(animation_controller_1_matrix1_6),
    .matrix3_6(animation_controller_1_matrix3_6), .matrix5_6(animation_controller_1_matrix5_6),
    .matrix7_6(animation_controller_1_matrix7_6), .matrix9_6(animation_controller_1_matrix9_6),
    .matrix1_7(animation_controller_1_matrix1_7), .matrix3_7(animation_controller_1_matrix3_7),
    .matrix5_7(animation_controller_1_matrix5_7), .matrix7_7(animation_controller_1_matrix7_7),
    .matrix9_7(animation_controller_1_matrix9_7), .matrix1_8(animation_controller_1_matrix1_8),
    .matrix3_8(animation_controller_1_matrix3_8), .matrix5_8(animation_controller_1_matrix5_8),
    .matrix7_8(animation_controller_1_matrix7_8), .matrix9_8(animation_controller_1_matrix9_8),
    .matrix1_9(animation_controller_1_matrix1_9), .matrix3_9(animation_controller_1_matrix3_9),
    .matrix5_9(animation_controller_1_matrix5_9), .matrix7_9(animation_controller_1_matrix7_9),
    .matrix9_9(animation_controller_1_matrix9_9), .control(result), .matrix2(animation_controller_1_matrix2),
    .matrix4(animation_controller_1_matrix4), .matrix6(animation_controller_1_matrix6),
    .matrix8(animation_controller_1_matrix8), .matrix10(animation_controller_1_matrix10),
    .matrix2_2(animation_controller_1_matrix2_2), .matrix4_2(animation_controller_1_matrix4_2),
    .matrix6_2(animation_controller_1_matrix6_2), .matrix8_2(animation_controller_1_matrix8_2),
    .matrix10_2(animation_controller_1_matrix10_2), .matrix2_3(animation_controller_1_matrix2_3),
    .matrix4_3(animation_controller_1_matrix4_3), .matrix6_3(animation_controller_1_matrix6_3),
    .matrix8_3(animation_controller_1_matrix8_3), .matrix10_3(animation_controller_1_matrix10_3),
    .matrix2_4(animation_controller_1_matrix2_4), .matrix4_4(animation_controller_1_matrix4_4),
    .matrix6_4(animation_controller_1_matrix6_4), .matrix8_4(animation_controller_1_matrix8_4),
    .matrix10_4(animation_controller_1_matrix10_4), .matrix2_5(animation_controller_1_matrix2_5),
    .matrix4_5(animation_controller_1_matrix4_5), .matrix6_5(animation_controller_1_matrix6_5),
    .matrix8_5(animation_controller_1_matrix8_5), .matrix10_5(animation_controller_1_matrix10_5),
    .matrix2_6(animation_controller_1_matrix2_6), .matrix4_6(animation_controller_1_matrix4_6),
    .matrix6_6(animation_controller_1_matrix6_6), .matrix8_6(animation_controller_1_matrix8_6),
    .matrix10_6(animation_controller_1_matrix10_6), .matrix2_7(animation_controller_1_matrix2_7),
    .matrix4_7(animation_controller_1_matrix4_7), .matrix6_7(animation_controller_1_matrix6_7),
    .matrix8_7(animation_controller_1_matrix8_7), .matrix10_7(animation_controller_1_matrix10_7),
    .matrix2_8(animation_controller_1_matrix2_8), .matrix4_8(animation_controller_1_matrix4_8),
    .matrix6_8(animation_controller_1_matrix6_8), .matrix8_8(animation_controller_1_matrix8_8),
    .matrix10_8(animation_controller_1_matrix10_8), .matrix2_9(animation_controller_1_matrix2_9),
    .matrix4_9(animation_controller_1_matrix4_9), .matrix6_9(animation_controller_1_matrix6_9),
    .matrix8_9(animation_controller_1_matrix8_9), .matrix10_9(animation_controller_1_matrix10_9));
  DotMatrix #(.matrixcols(9), .matrixrows(9)) dotmatrix_9 (
    .col0(backend_1_matrix4), .col1(backend_1_matrix4_2), .col2(backend_1_matrix4_3),
    .col3(backend_1_matrix4_4), .col4(backend_1_matrix4_5), .col5(backend_1_matrix4_6),
    .col6(backend_1_matrix4_7), .col7(backend_1_matrix4_8), .col8(backend_1_matrix4_9));
  Button T (.out(btT));
  Button R (.out(btR));
  Button U (.out(btU));
  Button Y (.out(btY));
  Button J (.out(btJ));
  Button F (.out(btF));
  Button H (.out(btH));
  Button G (.out(btG));
  Button B (.out(btB));
  Button C (.out(btC));
  Button V (.out(btV));
  Button N (.out(btN));
  DotMatrix #(.matrixcols(9), .matrixrows(9)) dotmatrix_10 (
    .col0(animation_controller_1_matrix6), .col1(animation_controller_1_matrix6_2),
    .col2(animation_controller_1_matrix6_3), .col3(animation_controller_1_matrix6_4),
    .col4(animation_controller_1_matrix6_5), .col5(animation_controller_1_matrix6_6),
    .col6(animation_controller_1_matrix6_7), .col7(animation_controller_1_matrix6_8),
    .col8(animation_controller_1_matrix6_9));
  DotMatrix #(.matrixcols(9), .matrixrows(9)) dotmatrix_11 (
    .col0(backend_1_matrix5_9), .col1(backend_1_matrix5_8), .col2(backend_1_matrix5_7),
    .col3(backend_1_matrix5_6), .col4(backend_1_matrix5_5), .col5(backend_1_matrix5_4),
    .col6(backend_1_matrix5_3), .col7(backend_1_matrix5_2), .col8(backend_1_matrix5));
  Button P (.out(btP));
  Button I (.out(btI));
  Button O (.out(btO));
  Button K (.out(btK));
  Button L (.out(btL));
  Button M (.out(btM));
  DotMatrix #(.matrixcols(9), .matrixrows(9)) dotmatrix_12 (
    .col0(animation_controller_1_matrix7_9), .col1(animation_controller_1_matrix7_8),
    .col2(animation_controller_1_matrix7_7), .col3(animation_controller_1_matrix7_6),
    .col4(animation_controller_1_matrix7_5), .col5(animation_controller_1_matrix7_4),
    .col6(animation_controller_1_matrix7_3), .col7(animation_controller_1_matrix7_2),
    .col8(animation_controller_1_matrix7));
  DotMatrix #(.matrixcols(9), .matrixrows(9)) dotmatrix_13 (
    .col0(backend_1_matrix6), .col1(backend_1_matrix6_2), .col2(backend_1_matrix6_3),
    .col3(backend_1_matrix6_4), .col4(backend_1_matrix6_5), .col5(backend_1_matrix6_6),
    .col6(backend_1_matrix6_7), .col7(backend_1_matrix6_8), .col8(backend_1_matrix6_9));
  LED led_1 (.in(halt));
  Button u_Enter (.out(enter));
  DotMatrix #(.matrixcols(9), .matrixrows(9)) dotmatrix_14 (
    .col0(animation_controller_1_matrix8), .col1(animation_controller_1_matrix8_2),
    .col2(animation_controller_1_matrix8_3), .col3(animation_controller_1_matrix8_4),
    .col4(animation_controller_1_matrix8_5), .col5(animation_controller_1_matrix8_6),
    .col6(animation_controller_1_matrix8_7), .col7(animation_controller_1_matrix8_8),
    .col8(animation_controller_1_matrix8_9));
  DotMatrix #(.matrixcols(9), .matrixrows(9)) dotmatrix_15 (
    .col0(backend_1_matrix7_9), .col1(backend_1_matrix7_8), .col2(backend_1_matrix7_7),
    .col3(backend_1_matrix7_6), .col4(backend_1_matrix7_5), .col5(backend_1_matrix7_4),
    .col6(backend_1_matrix7_3), .col7(backend_1_matrix7_2), .col8(backend_1_matrix7));
  DotMatrix #(.matrixcols(9), .matrixrows(9)) dotmatrix_16 (
    .col0(basic_switch_1_output), .col1(basic_switch_1_output_2), .col2(basic_switch_1_output_3),
    .col3(basic_switch_1_output_4), .col4(basic_switch_1_output_5), .col5(basic_switch_1_output_6),
    .col6(basic_switch_1_output_7), .col7(basic_switch_1_output_8), .col8(basic_switch_1_output_9));
  Basic_switch basic_switch_1 (
    .Let(\let ), .Output(basic_switch_1_output), .Output_2(basic_switch_1_output_2),
    .Output_3(basic_switch_1_output_3), .Output_4(basic_switch_1_output_4),
    .Output_5(basic_switch_1_output_5), .Output_6(basic_switch_1_output_6),
    .Output_7(basic_switch_1_output_7), .Output_8(basic_switch_1_output_8), .Output_9(basic_switch_1_output_9));
  DotMatrix #(.matrixcols(9), .matrixrows(9)) dotmatrix_17 (
    .col0(animation_controller_1_matrix9_9), .col1(animation_controller_1_matrix9_8),
    .col2(animation_controller_1_matrix9_7), .col3(animation_controller_1_matrix9_6),
    .col4(animation_controller_1_matrix9_5), .col5(animation_controller_1_matrix9_4),
    .col6(animation_controller_1_matrix9_3), .col7(animation_controller_1_matrix9_2),
    .col8(animation_controller_1_matrix9));
  DotMatrix #(.matrixcols(9), .matrixrows(9)) dotmatrix_18 (
    .col0(backend_1_matrix8), .col1(backend_1_matrix8_2), .col2(backend_1_matrix8_3),
    .col3(backend_1_matrix8_4), .col4(backend_1_matrix8_5), .col5(backend_1_matrix8_6),
    .col6(backend_1_matrix8_7), .col7(backend_1_matrix8_8), .col8(backend_1_matrix8_9));
  DotMatrix #(.matrixcols(9), .matrixrows(9)) dotmatrix_19 (
    .col0(animation_controller_1_matrix10), .col1(animation_controller_1_matrix10_2),
    .col2(animation_controller_1_matrix10_3), .col3(animation_controller_1_matrix10_4),
    .col4(animation_controller_1_matrix10_5), .col5(animation_controller_1_matrix10_6),
    .col6(animation_controller_1_matrix10_7), .col7(animation_controller_1_matrix10_8),
    .col8(animation_controller_1_matrix10_9));
  Backend backend_1 (
    .matrix1(backend_1_matrix1), .matrix3(backend_1_matrix3), .matrix5(backend_1_matrix5),
    .matrix7(backend_1_matrix7), .matrix1_2(backend_1_matrix1_2), .matrix3_2(backend_1_matrix3_2),
    .matrix5_2(backend_1_matrix5_2), .matrix7_2(backend_1_matrix7_2), .matrix1_3(backend_1_matrix1_3),
    .matrix3_3(backend_1_matrix3_3), .matrix5_3(backend_1_matrix5_3), .matrix7_3(backend_1_matrix7_3),
    .matrix1_4(backend_1_matrix1_4), .matrix3_4(backend_1_matrix3_4), .matrix5_4(backend_1_matrix5_4),
    .matrix7_4(backend_1_matrix7_4), .matrix1_5(backend_1_matrix1_5), .matrix3_5(backend_1_matrix3_5),
    .matrix5_5(backend_1_matrix5_5), .matrix7_5(backend_1_matrix7_5), .matrix1_6(backend_1_matrix1_6),
    .matrix3_6(backend_1_matrix3_6), .matrix5_6(backend_1_matrix5_6), .matrix7_6(backend_1_matrix7_6),
    .matrix1_7(backend_1_matrix1_7), .matrix3_7(backend_1_matrix3_7), .matrix5_7(backend_1_matrix5_7),
    .matrix7_7(backend_1_matrix7_7), .matrix1_8(backend_1_matrix1_8), .matrix3_8(backend_1_matrix3_8),
    .matrix5_8(backend_1_matrix5_8), .matrix7_8(backend_1_matrix7_8), .matrix1_9(backend_1_matrix1_9),
    .matrix3_9(backend_1_matrix3_9), .matrix5_9(backend_1_matrix5_9), .matrix7_9(backend_1_matrix7_9),
    .matrix2(backend_1_matrix2), .matrix4(backend_1_matrix4), .matrix6(backend_1_matrix6),
    .matrix8(backend_1_matrix8), .matrix2_2(backend_1_matrix2_2), .matrix4_2(backend_1_matrix4_2),
    .matrix6_2(backend_1_matrix6_2), .matrix8_2(backend_1_matrix8_2), .matrix2_3(backend_1_matrix2_3),
    .matrix4_3(backend_1_matrix4_3), .matrix6_3(backend_1_matrix6_3), .matrix8_3(backend_1_matrix8_3),
    .matrix2_4(backend_1_matrix2_4), .matrix4_4(backend_1_matrix4_4), .matrix6_4(backend_1_matrix6_4),
    .matrix8_4(backend_1_matrix8_4), .matrix2_5(backend_1_matrix2_5), .matrix4_5(backend_1_matrix4_5),
    .matrix6_5(backend_1_matrix6_5), .matrix8_5(backend_1_matrix8_5), .matrix2_6(backend_1_matrix2_6),
    .matrix4_6(backend_1_matrix4_6), .matrix6_6(backend_1_matrix6_6), .matrix8_6(backend_1_matrix8_6),
    .matrix2_7(backend_1_matrix2_7), .matrix4_7(backend_1_matrix4_7), .matrix6_7(backend_1_matrix6_7),
    .matrix8_7(backend_1_matrix8_7), .matrix2_8(backend_1_matrix2_8), .matrix4_8(backend_1_matrix4_8),
    .matrix6_8(backend_1_matrix6_8), .matrix8_8(backend_1_matrix8_8), .matrix2_9(backend_1_matrix2_9),
    .matrix4_9(backend_1_matrix4_9), .matrix6_9(backend_1_matrix6_9), .matrix8_9(backend_1_matrix8_9),
    .display(backend_1_display), .halt(halt), .\let (\let ), .enter(enter), .btA(btA), .btB(btB), .btC(btC),
    .btD(btD), .btE(btE), .btF(btF), .btG(btG), .btH(btH), .btI(btI), .btJ(btJ), .btK(btK), .btL(btL),
    .btM(btM), .btN(btN), .btO(btO), .btP(btP), .btQ(btQ), .btR(btR), .btS(btS), .btT(btT), .btU(btU),
    .btV(btV), .btW(btW), .btX(btX), .btY(btY), .btZ(btZ), .reset(reset), .result(result));

  // Notes on the sheet:
  //   LIVES
  //   When the light is ON, choose the letter and press the Enter button
endmodule

module Backend (
  input  reset,
  input  enter,
  input  btA,
  input  btB,
  input  btC,
  input  btD,
  input  btE,
  input  btF,
  input  btG,
  input  btH,
  input  btI,
  input  btJ,
  input  btK,
  input  btL,
  input  btM,
  input  btN,
  input  btO,
  input  btP,
  input  btQ,
  input  btR,
  input  btS,
  input  btT,
  input  btU,
  input  btV,
  input  btW,
  input  btX,
  input  btY,
  input  btZ,
  output [8:0] matrix1,
  output [8:0] matrix2,
  output [8:0] matrix3,
  output [8:0] matrix4,
  output [8:0] matrix5,
  output [8:0] matrix6,
  output [8:0] matrix7,
  output [8:0] matrix8,
  output [8:0] matrix1_2,
  output [8:0] matrix2_2,
  output [8:0] matrix3_2,
  output [8:0] matrix4_2,
  output [8:0] matrix5_2,
  output [8:0] matrix6_2,
  output [8:0] matrix7_2,
  output [8:0] matrix8_2,
  output [8:0] matrix1_3,
  output [8:0] matrix2_3,
  output [8:0] matrix3_3,
  output [8:0] matrix4_3,
  output [8:0] matrix5_3,
  output [8:0] matrix6_3,
  output [8:0] matrix7_3,
  output [8:0] matrix8_3,
  output [8:0] matrix1_4,
  output [8:0] matrix2_4,
  output [8:0] matrix3_4,
  output [8:0] matrix4_4,
  output [8:0] matrix5_4,
  output [8:0] matrix6_4,
  output [8:0] matrix7_4,
  output [8:0] matrix8_4,
  output [8:0] matrix1_5,
  output [8:0] matrix2_5,
  output [8:0] matrix3_5,
  output [8:0] matrix4_5,
  output [8:0] matrix5_5,
  output [8:0] matrix6_5,
  output [8:0] matrix7_5,
  output [8:0] matrix8_5,
  output [8:0] matrix1_6,
  output [8:0] matrix2_6,
  output [8:0] matrix3_6,
  output [8:0] matrix4_6,
  output [8:0] matrix5_6,
  output [8:0] matrix6_6,
  output [8:0] matrix7_6,
  output [8:0] matrix8_6,
  output [8:0] matrix1_7,
  output [8:0] matrix2_7,
  output [8:0] matrix3_7,
  output [8:0] matrix4_7,
  output [8:0] matrix5_7,
  output [8:0] matrix6_7,
  output [8:0] matrix7_7,
  output [8:0] matrix8_7,
  output [8:0] matrix1_8,
  output [8:0] matrix2_8,
  output [8:0] matrix3_8,
  output [8:0] matrix4_8,
  output [8:0] matrix5_8,
  output [8:0] matrix6_8,
  output [8:0] matrix7_8,
  output [8:0] matrix8_8,
  output [8:0] matrix1_9,
  output [8:0] matrix2_9,
  output [8:0] matrix3_9,
  output [8:0] matrix4_9,
  output [8:0] matrix5_9,
  output [8:0] matrix6_9,
  output [8:0] matrix7_9,
  output [8:0] matrix8_9,
  output [3:0] display,
  output [7:0] result,
  output halt,
  output [4:0] \let 
);

  wire and_1_out, and_2_out, cdm_8_mark5_1_p3, cdm_8_mark5_1_p4, cdm_8_mark5_1_p5, cdm_8_mark5_1_p7,
       cdm_8_mark5_1_p9, cdm_8_mark5_1_p10, cdm_8_mark5_1_p11, cdm_8_mark5_1_p12, cl, code, data, gen, GO,
       kcl, ld, ldf, n0_1_p2, n1_1_p2, n2_1_p2, n3_1_p2, n4_1_p2, n5_1_p2, n6_1_p2, n7_1_p2, not_1_out,
       or_1_out, or_2_out, rd_wr, WIN;
  wire [3:0] adr;
  wire [4:0] bt, random_1_out, wrd;
  wire [7:0] adder_1_out, cdm_8_mark5_1_p14, cdm_8_mark5_1_p15, cdm_8_mark5_1_p16, controlled_buffer_2_out,
       ram_adress_controller_1_out, rom_2_data;
  wire [7:4] counter_1_out;
  wire [8:0] switch_3_0_1_output, switch_3_0_1_output_2, switch_3_0_1_output_3, switch_3_0_1_output_4,
       switch_3_0_1_output_5, switch_3_0_1_output_6, switch_3_0_1_output_7, switch_3_0_1_output_8,
       switch_3_0_1_output_9, switch_3_0_2_output, switch_3_0_2_output_2, switch_3_0_2_output_3,
       switch_3_0_2_output_4, switch_3_0_2_output_5, switch_3_0_2_output_6, switch_3_0_2_output_7,
       switch_3_0_2_output_8, switch_3_0_2_output_9, switch_3_0_3_output, switch_3_0_3_output_2,
       switch_3_0_3_output_3, switch_3_0_3_output_4, switch_3_0_3_output_5, switch_3_0_3_output_6,
       switch_3_0_3_output_7, switch_3_0_3_output_8, switch_3_0_3_output_9, switch_3_0_4_output,
       switch_3_0_4_output_2, switch_3_0_4_output_3, switch_3_0_4_output_4, switch_3_0_4_output_5,
       switch_3_0_4_output_6, switch_3_0_4_output_7, switch_3_0_4_output_8, switch_3_0_4_output_9,
       switch_3_0_5_output, switch_3_0_5_output_2, switch_3_0_5_output_3, switch_3_0_5_output_4,
       switch_3_0_5_output_5, switch_3_0_5_output_6, switch_3_0_5_output_7, switch_3_0_5_output_8,
       switch_3_0_5_output_9, switch_3_0_6_output, switch_3_0_6_output_2, switch_3_0_6_output_3,
       switch_3_0_6_output_4, switch_3_0_6_output_5, switch_3_0_6_output_6, switch_3_0_6_output_7,
       switch_3_0_6_output_8, switch_3_0_6_output_9, switch_3_0_7_output, switch_3_0_7_output_2,
       switch_3_0_7_output_3, switch_3_0_7_output_4, switch_3_0_7_output_5, switch_3_0_7_output_6,
       switch_3_0_7_output_7, switch_3_0_7_output_8, switch_3_0_7_output_9, switch_3_0_8_output,
       switch_3_0_8_output_2, switch_3_0_8_output_3, switch_3_0_8_output_4, switch_3_0_8_output_5,
       switch_3_0_8_output_6, switch_3_0_8_output_7, switch_3_0_8_output_8, switch_3_0_8_output_9;

  Switch_3_0 switch_3_0_1 (
    .ctrl(result[7]), .GOLet(5'b00111), .Let(wrd), .Output(switch_3_0_1_output),
    .Output_2(switch_3_0_1_output_2), .Output_3(switch_3_0_1_output_3), .Output_4(switch_3_0_1_output_4),
    .Output_5(switch_3_0_1_output_5), .Output_6(switch_3_0_1_output_6), .Output_7(switch_3_0_1_output_7),
    .Output_8(switch_3_0_1_output_8), .Output_9(switch_3_0_1_output_9), .clock(n7_1_p2), .reset(reset),
    .Win(WIN), .WINLet(5'b11001), .Game_over(GO), .gen(gen));
  Life_cntr life_cntr_1 (.Game_over(GO), .flags(result), .display(display), .clock(halt), .reset(reset), .start(halt));
  Comparator comparator_1 (.a(result), .b({8{1'b1}}), .eq(WIN));  // open: gt, lt
  Switch_addition switch_addition_1 (
    .fl(ldf), .\let (5'b00100), .input_10(matrix1_9), .input_11(matrix1_8), .input_12(matrix1_7),
    .input_13(matrix1_6), .input_14(matrix1_5), .input_15(matrix1_4), .input_16(matrix1_3),
    .input_17(matrix1_2), .input_18(matrix1), .\input (switch_3_0_1_output), .input_2(switch_3_0_1_output_2),
    .input_3(switch_3_0_1_output_3), .input_4(switch_3_0_1_output_4), .input_5(switch_3_0_1_output_5),
    .input_6(switch_3_0_1_output_6), .input_7(switch_3_0_1_output_7), .input_8(switch_3_0_1_output_8),
    .input_9(switch_3_0_1_output_9));
  // _7 7_1: pin names not known; wires that end beside it: ld, n7_1_p2, adr
  Switch_addition switch_addition_2 (
    .fl(ldf), .\let (5'b01111), .input_10(matrix2), .input_11(matrix2_2), .input_12(matrix2_3),
    .input_13(matrix2_4), .input_14(matrix2_5), .input_15(matrix2_6), .input_16(matrix2_7),
    .input_17(matrix2_8), .input_18(matrix2_9), .\input (switch_3_0_2_output),
    .input_2(switch_3_0_2_output_2), .input_3(switch_3_0_2_output_3), .input_4(switch_3_0_2_output_4),
    .input_5(switch_3_0_2_output_5), .input_6(switch_3_0_2_output_6), .input_7(switch_3_0_2_output_7),
    .input_8(switch_3_0_2_output_8), .input_9(switch_3_0_2_output_9));
  Switch_3_0 switch_3_0_2 (
    .ctrl(result[6]), .GOLet(5'b00001), .Let(wrd), .Output(switch_3_0_2_output),
    .Output_2(switch_3_0_2_output_2), .Output_3(switch_3_0_2_output_3), .Output_4(switch_3_0_2_output_4),
    .Output_5(switch_3_0_2_output_5), .Output_6(switch_3_0_2_output_6), .Output_7(switch_3_0_2_output_7),
    .Output_8(switch_3_0_2_output_8), .Output_9(switch_3_0_2_output_9), .clock(n6_1_p2), .reset(reset),
    .Win(WIN), .WINLet(5'b01111), .Game_over(GO), .gen(gen));
  // _6 6_1: pin names not known; wires that end beside it: ld, n6_1_p2, adr
  Clock clock_1 (.out(gen));
  or or_1 (or_1_out, WIN, GO);
  Transistor transistor_1 (.in(gen), .out(cl), .gate(or_1_out));
  Random #(.width(5)) random_1 (.clk(cl), .next(reset), .out(random_1_out));  // open: clr
  // Probe on random_1_out
  Register #(.width(5)) register_1 (.D(bt), .Q(\let ), .clk(kcl), .clr(reset));  // open: en
  // Probe on \let 
  Pull_Resistor pull_resistor_1 (.node(kcl));
  Pull_Resistor pull_resistor_2 (.node(ld));
  Transistor #(.gate("br")) transistor_2 (.in(cl), .out(ld), .gate(ldf));
  Adder adder_1 (.a({4'b0000, adr}), .b({random_1_out, 3'b000}), .out(adder_1_out));  // open: cin, cout
  Switch_addition switch_addition_3 (
    .fl(ldf), .\let (5'b01111), .input_10(matrix3_9), .input_11(matrix3_8), .input_12(matrix3_7),
    .input_13(matrix3_6), .input_14(matrix3_5), .input_15(matrix3_4), .input_16(matrix3_3),
    .input_17(matrix3_2), .input_18(matrix3), .\input (switch_3_0_3_output), .input_2(switch_3_0_3_output_2),
    .input_3(switch_3_0_3_output_3), .input_4(switch_3_0_3_output_4), .input_5(switch_3_0_3_output_5),
    .input_6(switch_3_0_3_output_6), .input_7(switch_3_0_3_output_7), .input_8(switch_3_0_3_output_8),
    .input_9(switch_3_0_3_output_9));
  Switch_3_0 switch_3_0_3 (
    .ctrl(result[5]), .GOLet(5'b01101), .Let(wrd), .Output(switch_3_0_3_output),
    .Output_2(switch_3_0_3_output_2), .Output_3(switch_3_0_3_output_3), .Output_4(switch_3_0_3_output_4),
    .Output_5(switch_3_0_3_output_5), .Output_6(switch_3_0_3_output_6), .Output_7(switch_3_0_3_output_7),
    .Output_8(switch_3_0_3_output_8), .Output_9(switch_3_0_3_output_9), .clock(n5_1_p2), .reset(reset),
    .Win(WIN), .WINLet(5'b10101), .Game_over(GO), .gen(gen));
  Counter counter_1 (.Max(8'h7), .out({counter_1_out, adr}), .\end (ldf), .clock(cl), .reset(reset));
  Transistor #(.\type ("n"), .width(5)) transistor_3 (.in(5'b00001), .out(bt), .gate(btA));
  Transistor #(.\type ("n"), .width(5)) transistor_4 (.in(5'b00010), .out(bt), .gate(btB));
  buf buffer_1 (kcl, btA);
  Transistor #(.\type ("n"), .width(5)) transistor_5 (.in(5'b01110), .out(bt), .gate(btN));
  Transistor #(.\type ("n"), .width(5)) transistor_6 (.in(5'b01111), .out(bt), .gate(btO));
  buf buffer_2 (kcl, btN);
  Switch_3_0 switch_3_0_4 (
    .ctrl(result[4]), .GOLet(5'b00101), .Let(wrd), .Output(switch_3_0_4_output),
    .Output_2(switch_3_0_4_output_2), .Output_3(switch_3_0_4_output_3), .Output_4(switch_3_0_4_output_4),
    .Output_5(switch_3_0_4_output_5), .Output_6(switch_3_0_4_output_6), .Output_7(switch_3_0_4_output_7),
    .Output_8(switch_3_0_4_output_8), .Output_9(switch_3_0_4_output_9), .clock(n4_1_p2), .reset(reset),
    .Win(WIN), .WINLet({5{1'b0}}), .Game_over(GO), .gen(gen));
  // _5 5_1: pin names not known; wires that end beside it: ld, n5_1_p2, adr
  ROM #(.dataWidth(5)) rom_1 (.addr(adder_1_out), .data(wrd));  // open: sel
  Transistor #(.\type ("n"), .width(5)) transistor_7 (.in(5'b00011), .out(bt), .gate(btC));
  buf buffer_3 (kcl, btB);
  buf buffer_4 (kcl, btC);
  Transistor #(.\type ("n"), .width(5)) transistor_8 (.in(5'b10000), .out(bt), .gate(btP));
  buf buffer_5 (kcl, btP);
  buf buffer_6 (kcl, btO);
  Switch_addition switch_addition_4 (
    .fl(ldf), .\let (5'b10010), .input_10(matrix4), .input_11(matrix4_2), .input_12(matrix4_3),
    .input_13(matrix4_4), .input_14(matrix4_5), .input_15(matrix4_6), .input_16(matrix4_7),
    .input_17(matrix4_8), .input_18(matrix4_9), .\input (switch_3_0_4_output),
    .input_2(switch_3_0_4_output_2), .input_3(switch_3_0_4_output_3), .input_4(switch_3_0_4_output_4),
    .input_5(switch_3_0_4_output_5), .input_6(switch_3_0_4_output_6), .input_7(switch_3_0_4_output_7),
    .input_8(switch_3_0_4_output_8), .input_9(switch_3_0_4_output_9));
  // _4 4_1: pin names not known; wires that end beside it: ld, n4_1_p2, adr
  Transistor #(.\type ("n"), .width(5)) transistor_9 (.in(5'b00100), .out(bt), .gate(btD));
  buf buffer_7 (kcl, btD);
  Transistor #(.\type ("n"), .width(5)) transistor_10 (.in(5'b10001), .out(bt), .gate(btQ));
  buf buffer_8 (kcl, btQ);
  // Probe on cdm_8_mark5_1_p4
  // Probe on cdm_8_mark5_1_p3
  Transistor #(.\type ("n")) transistor_11 (.in(cl), .gate(and_1_out));  // open: out
  and and_1 (and_1_out, ldf, ~halt);  // AND_Gate
  Transistor #(.\type ("n"), .width(5)) transistor_12 (.in(5'b00110), .out(bt), .gate(btF));
  Transistor #(.\type ("n"), .width(5)) transistor_13 (.in(5'b00101), .out(bt), .gate(btE));
  buf buffer_9 (kcl, btE);
  Transistor #(.\type ("n"), .width(5)) transistor_14 (.in(5'b10011), .out(bt), .gate(btS));
  Transistor #(.\type ("n"), .width(5)) transistor_15 (.in(5'b10010), .out(bt), .gate(btR));
  buf buffer_10 (kcl, btR);
  // Probe on cdm_8_mark5_1_p7
  // Probe on cdm_8_mark5_1_p10
  // Probe on cdm_8_mark5_1_p9
  // Probe on cdm_8_mark5_1_p5
  Transistor #(.\type ("n"), .width(5)) transistor_16 (.in(5'b00111), .out(bt), .gate(btG));
  buf buffer_11 (kcl, btG);
  buf buffer_12 (kcl, btF);
  Transistor #(.\type ("n"), .width(5)) transistor_17 (.in(5'b10100), .out(bt), .gate(btT));
  buf buffer_13 (kcl, btS);
  buf buffer_14 (kcl, btT);
  // CdM_8_mark5 cdm_8_mark5_1: pin names not known; wires that end beside it: reset, result, cdm_8_mark5_1_p3, cdm_8_mark5_1_p4, cdm_8_mark5_1_p5, halt, cdm_8_mark5_1_p7, enter, cdm_8_mark5_1_p9, cdm_8_mark5_1_p10, cdm_8_mark5_1_p11, cdm_8_mark5_1_p12, rd_wr, cdm_8_mark5_1_p14, cdm_8_mark5_1_p15, cdm_8_mark5_1_p16
  not not_1 (not_1_out, rd_wr);
  assign cdm_8_mark5_1_p16 = rd_wr ? controlled_buffer_2_out : 8'bz;  // Controlled_Buffer controlled_buffer_1
  Transistor #(.\type ("n"), .width(5)) transistor_18 (.in(5'b01000), .out(bt), .gate(btH));
  buf buffer_15 (kcl, btH);
  Transistor #(.\type ("n"), .width(5)) transistor_19 (.in(5'b10101), .out(bt), .gate(btU));
  buf buffer_16 (kcl, btU);
  Switch_addition switch_addition_5 (
    .fl(ldf), .\let (5'b00111), .input_10(matrix5_9), .input_11(matrix5_8), .input_12(matrix5_7),
    .input_13(matrix5_6), .input_14(matrix5_5), .input_15(matrix5_4), .input_16(matrix5_3),
    .input_17(matrix5_2), .input_18(matrix5), .\input (switch_3_0_5_output), .input_2(switch_3_0_5_output_2),
    .input_3(switch_3_0_5_output_3), .input_4(switch_3_0_5_output_4), .input_5(switch_3_0_5_output_5),
    .input_6(switch_3_0_5_output_6), .input_7(switch_3_0_5_output_7), .input_8(switch_3_0_5_output_8),
    .input_9(switch_3_0_5_output_9));
  Switch_3_0 switch_3_0_5 (
    .ctrl(result[3]), .GOLet(5'b01111), .Let(wrd), .Output(switch_3_0_5_output),
    .Output_2(switch_3_0_5_output_2), .Output_3(switch_3_0_5_output_3), .Output_4(switch_3_0_5_output_4),
    .Output_5(switch_3_0_5_output_5), .Output_6(switch_3_0_5_output_6), .Output_7(switch_3_0_5_output_7),
    .Output_8(switch_3_0_5_output_8), .Output_9(switch_3_0_5_output_9), .clock(n3_1_p2), .reset(reset),
    .Win(WIN), .WINLet(5'b10111), .Game_over(GO), .gen(gen));
  // _3 3_1: pin names not known; wires that end beside it: ld, n3_1_p2, adr
  Pull_Resistor pull_resistor_3 (.node(code));
  Pull_Resistor pull_resistor_4 (.node(data));
  Decoder decoder_1 (.out0(code), .out1(data), .sel(cdm_8_mark5_1_p11), .en(cdm_8_mark5_1_p12));
  assign controlled_buffer_2_out = not_1_out ? cdm_8_mark5_1_p15 : 8'bz;  // Controlled_Buffer controlled_buffer_2
  Transistor #(.\type ("n"), .width(5)) transistor_20 (.in(5'b01001), .out(bt), .gate(btI));
  Transistor #(.\type ("n"), .width(5)) transistor_21 (.in(5'b01010), .out(bt), .gate(btJ));
  buf buffer_17 (kcl, btI);
  Transistor #(.\type ("n"), .width(5)) transistor_22 (.in(5'b10111), .out(bt), .gate(btW));
  Transistor #(.\type ("n"), .width(5)) transistor_23 (.in(5'b10110), .out(bt), .gate(btV));
  buf buffer_18 (kcl, btV);
  Switch_addition switch_addition_6 (
    .fl(ldf), .\let (5'b00001), .input_10(matrix6), .input_11(matrix6_2), .input_12(matrix6_3),
    .input_13(matrix6_4), .input_14(matrix6_5), .input_15(matrix6_6), .input_16(matrix6_7),
    .input_17(matrix6_8), .input_18(matrix6_9), .\input (switch_3_0_6_output),
    .input_2(switch_3_0_6_output_2), .input_3(switch_3_0_6_output_3), .input_4(switch_3_0_6_output_4),
    .input_5(switch_3_0_6_output_5), .input_6(switch_3_0_6_output_6), .input_7(switch_3_0_6_output_7),
    .input_8(switch_3_0_6_output_8), .input_9(switch_3_0_6_output_9));
  Switch_3_0 switch_3_0_6 (
    .ctrl(result[2]), .GOLet(5'b10110), .Let(wrd), .Output(switch_3_0_6_output),
    .Output_2(switch_3_0_6_output_2), .Output_3(switch_3_0_6_output_3), .Output_4(switch_3_0_6_output_4),
    .Output_5(switch_3_0_6_output_5), .Output_6(switch_3_0_6_output_6), .Output_7(switch_3_0_6_output_7),
    .Output_8(switch_3_0_6_output_8), .Output_9(switch_3_0_6_output_9), .clock(n2_1_p2), .reset(reset),
    .Win(WIN), .WINLet(5'b01001), .Game_over(GO), .gen(gen));
  RAM_adress_controller ram_adress_controller_1 (
    .proc(cdm_8_mark5_1_p14), .word_load(adr), .out(ram_adress_controller_1_out), .word_loaded(ldf),
    .halt(halt));
  or or_2 (or_2_out, data, ~ldf, halt);  // OR_Gate
  Transistor #(.\type ("n"), .width(5)) transistor_24 (.in(5'b01011), .out(bt), .gate(btK));
  buf buffer_19 (kcl, btK);
  buf buffer_20 (kcl, btJ);
  Transistor #(.\type ("n"), .width(5)) transistor_25 (.in(5'b11000), .out(bt), .gate(btX));
  buf buffer_21 (kcl, btW);
  buf buffer_22 (kcl, btX);
  // _2 2_1: pin names not known; wires that end beside it: ld, n2_1_p2, adr
  ROM rom_2 (.addr(cdm_8_mark5_1_p14), .data(rom_2_data), .sel(code));
  RAM ram_1 (
    .addr(ram_adress_controller_1_out), .data(controlled_buffer_2_out), .sel(or_2_out), .clk(cl),
    .ld(and_2_out), .clr(reset));
  and and_2 (and_2_out, ~halt, ldf, rd_wr);  // AND_Gate
  Transistor #(.\type ("n"), .width(5)) transistor_26 (.in(5'b01100), .out(bt), .gate(btL));
  buf buffer_23 (kcl, btL);
  Transistor #(.\type ("n"), .width(5)) transistor_27 (.in(5'b11001), .out(bt), .gate(btY));
  buf buffer_24 (kcl, btY);
  RAM_data_controller ram_data_controller_1 (
    .out(controlled_buffer_2_out), .proc(rom_2_data), .word(wrd), .letter(\let ), .word_loaded(ldf),
    .halt(halt));
  Transistor #(.\type ("n"), .width(5)) transistor_28 (.in(5'b01101), .out(bt), .gate(btM));
  buf buffer_25 (kcl, btM);
  Transistor #(.\type ("n"), .width(5)) transistor_29 (.in(5'b11010), .out(bt), .gate(btZ));
  buf buffer_26 (kcl, btZ);
  Switch_3_0 switch_3_0_7 (
    .ctrl(result[1]), .GOLet(5'b00101), .Let(wrd), .Output(switch_3_0_7_output),
    .Output_2(switch_3_0_7_output_2), .Output_3(switch_3_0_7_output_3), .Output_4(switch_3_0_7_output_4),
    .Output_5(switch_3_0_7_output_5), .Output_6(switch_3_0_7_output_6), .Output_7(switch_3_0_7_output_7),
    .Output_8(switch_3_0_7_output_8), .Output_9(switch_3_0_7_output_9), .clock(n1_1_p2), .reset(reset),
    .Win(WIN), .WINLet(5'b01110), .Game_over(GO), .gen(gen));
  Switch_addition switch_addition_7 (
    .fl(ldf), .\let (5'b01101), .input_10(matrix7_9), .input_11(matrix7_8), .input_12(matrix7_7),
    .input_13(matrix7_6), .input_14(matrix7_5), .input_15(matrix7_4), .input_16(matrix7_3),
    .input_17(matrix7_2), .input_18(matrix7), .\input (switch_3_0_7_output), .input_2(switch_3_0_7_output_2),
    .input_3(switch_3_0_7_output_3), .input_4(switch_3_0_7_output_4), .input_5(switch_3_0_7_output_5),
    .input_6(switch_3_0_7_output_6), .input_7(switch_3_0_7_output_7), .input_8(switch_3_0_7_output_8),
    .input_9(switch_3_0_7_output_9));
  Switch_3_0 switch_3_0_8 (
    .ctrl(result[0]), .GOLet(5'b10010), .Let(wrd), .Output(switch_3_0_8_output),
    .Output_2(switch_3_0_8_output_2), .Output_3(switch_3_0_8_output_3), .Output_4(switch_3_0_8_output_4),
    .Output_5(switch_3_0_8_output_5), .Output_6(switch_3_0_8_output_6), .Output_7(switch_3_0_8_output_7),
    .Output_8(switch_3_0_8_output_8), .Output_9(switch_3_0_8_output_9), .clock(n0_1_p2), .reset(reset),
    .Win(WIN), .WINLet(5'b11011), .Game_over(GO), .gen(gen));
  // _1 1_1: pin names not known; wires that end beside it: ld, n1_1_p2, adr
  Switch_addition switch_addition_8 (
    .fl(ldf), .\let (5'b00101), .input_10(matrix8), .input_11(matrix8_2), .input_12(matrix8_3),
    .input_13(matrix8_4), .input_14(matrix8_5), .input_15(matrix8_6), .input_16(matrix8_7),
    .input_17(matrix8_8), .input_18(matrix8_9), .\input (switch_3_0_8_output),
    .input_2(switch_3_0_8_output_2), .input_3(switch_3_0_8_output_3), .input_4(switch_3_0_8_output_4),
    .input_5(switch_3_0_8_output_5), .input_6(switch_3_0_8_output_6), .input_7(switch_3_0_8_output_7),
    .input_8(switch_3_0_8_output_8), .input_9(switch_3_0_8_output_9));
  // _0 0_1: pin names not known; wires that end beside it: ld, n0_1_p2, adr, reset

  // Other names for the same wires on the sheet: r0[7:0] = result

  // Notes on the sheet:
  //   Keyboard
  //   controller
  //   Clock & adress block
  //   Dictionary block
  //   buffer_1 drives only 1 and floats otherwise
  //   buffer_2 drives only 1 and floats otherwise
  //   contents of rom_1 (hex, n*v repeats v):
  //   1 2 13 f c 15 14 5 3 1 c 5 e 4 1 12 5 c 5 10 8 1 e 14 d f 15 e 14 1 9 e 10 1 12 1 4 9 13 5 15 c 14 9
  //   d 1 14 5 4 f 3 15 d 5 e 14 18 5 e f 10 8 f 2 3 f d 10 15 14 5 12 5 e 7 9 e 5 5 12 6 5 13 14 9 16 1 c
  //   4 9 13 3 f 16 5 12 e 1 16 9 7 1 14 5 f 10 5 12 1 14 f 12 7 5 e 5 12 1 14 5 10 9 3 14 15 12 5 13 2 15
  //   9 c 4 9 e 7 3 8 9 c 4 12 5 e 8 f 13 10 9 14 1 c b 9 14 3 8 5 e 13 c 1 e 7 15 1 7 5 d 9 13 14 1 b 5
  //   13 e f 14 5 2 f f b 10 1 9 e 14 9 e 7 11 15 5 13 14 9 f e 12 5 13 5 1 12 3 8 13 f 6 14 17 1 12 5 13
  //   14 12 1 14 5 7 19 14 12 1 9 e 9 e 7 16 1 3 1 14 9 f e 1 3 14 9 16 9 14 19 13 14 15 4 5 e 14 13
  //   buffer_3 drives only 1 and floats otherwise
  //   buffer_4 drives only 1 and floats otherwise
  //   buffer_5 drives only 1 and floats otherwise
  //   buffer_6 drives only 1 and floats otherwise
  //   buffer_7 drives only 1 and floats otherwise
  //   buffer_8 drives only 1 and floats otherwise
  //   buffer_9 drives only 1 and floats otherwise
  //   buffer_10 drives only 1 and floats otherwise
  //   Processor & memory blocks
  //   buffer_11 drives only 1 and floats otherwise
  //   buffer_12 drives only 1 and floats otherwise
  //   buffer_13 drives only 1 and floats otherwise
  //   buffer_14 drives only 1 and floats otherwise
  //   buffer_15 drives only 1 and floats otherwise
  //   buffer_16 drives only 1 and floats otherwise
  //   buffer_17 drives only 1 and floats otherwise
  //   buffer_18 drives only 1 and floats otherwise
  //   buffer_19 drives only 1 and floats otherwise
  //   buffer_20 drives only 1 and floats otherwise
  //   buffer_21 drives only 1 and floats otherwise
  //   buffer_22 drives only 1 and floats otherwise
  //   contents of rom_2 (hex, n*v repeats v):
  //   d1 80 c2 ba a e0 13 d3 9 bf 7b e1 e 54 c6 8e 91 ee 2 d4
  //   buffer_23 drives only 1 and floats otherwise
  //   buffer_24 drives only 1 and floats otherwise
  //   buffer_25 drives only 1 and floats otherwise
  //   buffer_26 drives only 1 and floats otherwise
endmodule

module Animation_Controller (
  input  [7:0] control,
  output [8:0] matrix1,
  output [8:0] matrix2,
  output [8:0] matrix3,
  output [8:0] matrix4,
  output [8:0] matrix5,
  output [8:0] matrix6,
  output [8:0] matrix7,
  output [8:0] matrix8,
  output [8:0] matrix9,
  output [8:0] matrix10,
  output [8:0] matrix1_2,
  output [8:0] matrix2_2,
  output [8:0] matrix3_2,
  output [8:0] matrix4_2,
  output [8:0] matrix5_2,
  output [8:0] matrix6_2,
  output [8:0] matrix7_2,
  output [8:0] matrix8_2,
  output [8:0] matrix9_2,
  output [8:0] matrix10_2,
  output [8:0] matrix1_3,
  output [8:0] matrix2_3,
  output [8:0] matrix3_3,
  output [8:0] matrix4_3,
  output [8:0] matrix5_3,
  output [8:0] matrix6_3,
  output [8:0] matrix7_3,
  output [8:0] matrix8_3,
  output [8:0] matrix9_3,
  output [8:0] matrix10_3,
  output [8:0] matrix1_4,
  output [8:0] matrix2_4,
  output [8:0] matrix3_4,
  output [8:0] matrix4_4,
  output [8:0] matrix5_4,
  output [8:0] matrix6_4,
  output [8:0] matrix7_4,
  output [8:0] matrix8_4,
  output [8:0] matrix9_4,
  output [8:0] matrix10_4,
  output [8:0] matrix1_5,
  output [8:0] matrix2_5,
  output [8:0] matrix3_5,
  output [8:0] matrix4_5,
  output [8:0] matrix5_5,
  output [8:0] matrix6_5,
  output [8:0] matrix7_5,
  output [8:0] matrix8_5,
  output [8:0] matrix9_5,
  output [8:0] matrix10_5,
  output [8:0] matrix1_6,
  output [8:0] matrix2_6,
  output [8:0] matrix3_6,
  output [8:0] matrix4_6,
  output [8:0] matrix5_6,
  output [8:0] matrix6_6,
  output [8:0] matrix7_6,
  output [8:0] matrix8_6,
  output [8:0] matrix9_6,
  output [8:0] matrix10_6,
  output [8:0] matrix1_7,
  output [8:0] matrix2_7,
  output [8:0] matrix3_7,
  output [8:0] matrix4_7,
  output [8:0] matrix5_7,
  output [8:0] matrix6_7,
  output [8:0] matrix7_7,
  output [8:0] matrix8_7,
  output [8:0] matrix9_7,
  output [8:0] matrix10_7,
  output [8:0] matrix1_8,
  output [8:0] matrix2_8,
  output [8:0] matrix3_8,
  output [8:0] matrix4_8,
  output [8:0] matrix5_8,
  output [8:0] matrix6_8,
  output [8:0] matrix7_8,
  output [8:0] matrix8_8,
  output [8:0] matrix9_8,
  output [8:0] matrix10_8,
  output [8:0] matrix1_9,
  output [8:0] matrix2_9,
  output [8:0] matrix3_9,
  output [8:0] matrix4_9,
  output [8:0] matrix5_9,
  output [8:0] matrix6_9,
  output [8:0] matrix7_9,
  output [8:0] matrix8_9,
  output [8:0] matrix9_9,
  output [8:0] matrix10_9
);

  wire clock_1_out;
  wire [1:0] tact_divider_1_out;
  wire [1:1] and_1_out, and_2_out, and_3_out, and_4_out, and_5_out, and_6_out, and_7_out;

  Animation_Switch animation_switch_1 (
    .Let({1'b0, control[7]}), .pos_1(3'b001), .pos_2(3'b000), .Output(matrix1_9), .Output_2(matrix1_8),
    .Output_3(matrix1_7), .Output_4(matrix1_6), .Output_5(matrix1_5), .Output_6(matrix1_4),
    .Output_7(matrix1_3), .Output_8(matrix1_2), .Output_9(matrix1));  // open: pos_3
  Animation_Switch animation_switch_2 (
    .Let({and_1_out[1], control[7]}), .pos_1(3'b100), .pos_2(3'b011), .pos_3(3'b101), .Output(matrix2),
    .Output_2(matrix2_2), .Output_3(matrix2_3), .Output_4(matrix2_4), .Output_5(matrix2_5),
    .Output_6(matrix2_6), .Output_7(matrix2_7), .Output_8(matrix2_8), .Output_9(matrix2_9));
  and and_1 (and_1_out[1], ~control[6], control[7]);  // AND_Gate
  Animation_Switch animation_switch_3 (
    .Let({and_2_out[1], control[6]}), .pos_1(3'b100), .pos_2(3'b011), .pos_3(3'b101), .Output(matrix3_9),
    .Output_2(matrix3_8), .Output_3(matrix3_7), .Output_4(matrix3_6), .Output_5(matrix3_5),
    .Output_6(matrix3_4), .Output_7(matrix3_3), .Output_8(matrix3_2), .Output_9(matrix3));
  and and_2 (and_2_out[1], control[7], ~control[5], control[6]);  // AND_Gate
  Animation_Switch animation_switch_4 (
    .Let({and_3_out[1], control[5]}), .pos_1(3'b100), .pos_2(3'b011), .pos_3(3'b101), .Output(matrix4),
    .Output_2(matrix4_2), .Output_3(matrix4_3), .Output_4(matrix4_4), .Output_5(matrix4_5),
    .Output_6(matrix4_6), .Output_7(matrix4_7), .Output_8(matrix4_8), .Output_9(matrix4_9));
  and and_3 (and_3_out[1], control[7], control[6], control[5], ~control[4]);  // AND_Gate
  Animation_Switch animation_switch_5 (
    .Let({and_4_out[1], control[4]}), .pos_1(3'b100), .pos_2(3'b011), .pos_3(3'b101), .Output(matrix5_9),
    .Output_2(matrix5_8), .Output_3(matrix5_7), .Output_4(matrix5_6), .Output_5(matrix5_5),
    .Output_6(matrix5_4), .Output_7(matrix5_3), .Output_8(matrix5_2), .Output_9(matrix5));
  and and_4 (and_4_out[1], control[7], control[6], control[5], control[4], ~control[3]);  // AND_Gate
  Animation_Switch animation_switch_6 (
    .Let({and_5_out[1], control[3]}), .pos_1(3'b100), .pos_2(3'b011), .pos_3(3'b101), .Output(matrix6),
    .Output_2(matrix6_2), .Output_3(matrix6_3), .Output_4(matrix6_4), .Output_5(matrix6_5),
    .Output_6(matrix6_6), .Output_7(matrix6_7), .Output_8(matrix6_8), .Output_9(matrix6_9));
  and and_5 (and_5_out[1], control[7], control[6], control[5], control[3], ~control[2], control[4]);  // AND_Gate
  Animation_Switch animation_switch_7 (
    .Let({and_6_out[1], control[2]}), .pos_1(3'b100), .pos_2(3'b011), .pos_3(3'b101), .Output(matrix7_9),
    .Output_2(matrix7_8), .Output_3(matrix7_7), .Output_4(matrix7_6), .Output_5(matrix7_5),
    .Output_6(matrix7_4), .Output_7(matrix7_3), .Output_8(matrix7_2), .Output_9(matrix7));
  and and_6 (and_6_out[1], control[7], control[6], control[5], control[4], control[2], ~control[1], control[3]);  // AND_Gate
  Animation_Switch animation_switch_8 (
    .Let({and_7_out[1], control[1]}), .pos_1(3'b100), .pos_2(3'b011), .pos_3(3'b101), .Output(matrix8),
    .Output_2(matrix8_2), .Output_3(matrix8_3), .Output_4(matrix8_4), .Output_5(matrix8_5),
    .Output_6(matrix8_6), .Output_7(matrix8_7), .Output_8(matrix8_8), .Output_9(matrix8_9));
  and and_7 (and_7_out[1], control[7], control[6], control[5], control[4], control[1], control[2], control[3], ~control[0]);  // AND_Gate
  Animation_Switch animation_switch_9 (
    .Let({1'b0, control[0]}), .pos_1(3'b100), .pos_2(3'b011), .Output(matrix9_9), .Output_2(matrix9_8),
    .Output_3(matrix9_7), .Output_4(matrix9_6), .Output_5(matrix9_5), .Output_6(matrix9_4),
    .Output_7(matrix9_3), .Output_8(matrix9_2), .Output_9(matrix9));  // open: pos_3
  Animation_Switch animation_switch_10 (
    .Let(tact_divider_1_out), .pos_1(3'b001), .pos_2(3'b010), .pos_3(3'b000), .Output(matrix10),
    .Output_2(matrix10_2), .Output_3(matrix10_3), .Output_4(matrix10_4), .Output_5(matrix10_5),
    .Output_6(matrix10_6), .Output_7(matrix10_7), .Output_8(matrix10_8), .Output_9(matrix10_9));
  nand nand_1 (tact_divider_1_out[1], control[7], control[6], control[5], control[4], control[3], control[2], control[1], control[0]);
  Tact_divider tact_divider_1 (.clock(clock_1_out), .out(tact_divider_1_out[0]));
  Clock clock_1 (.out(clock_1_out));
endmodule

module Animation_Switch (
  input  [2:0] pos_1,
  input  [2:0] pos_2,
  input  [2:0] pos_3,
  input  [1:0] Let,
  output [8:0] Output,
  output [8:0] Output_2,
  output [8:0] Output_3,
  output [8:0] Output_4,
  output [8:0] Output_5,
  output [8:0] Output_6,
  output [8:0] Output_7,
  output [8:0] Output_8,
  output [8:0] Output_9
);

  wire [26:0] multiplexer_1_out, multiplexer_3_out, multiplexer_4_out, multiplexer_5_out, multiplexer_6_out,
       multiplexer_8_out, multiplexer_9_out, multiplexer_11_out, multiplexer_12_out;

  Multiplexer #(.select(3), .width(27), .enable("false")) multiplexer_1 (
    .in0({27{1'b0}}), .in1(27'h6022), .in2(27'hc022), .in3(27'hfe80), .in4(27'hfea4), .in5(27'hfe90),
    .out(multiplexer_1_out), .sel(pos_1));  // open: in6, in7
  Multiplexer #(.select(2), .width(27), .enable("false")) multiplexer_2 (
    .in0(multiplexer_1_out), .in1(multiplexer_4_out), .in2(multiplexer_3_out), .in3(multiplexer_3_out),
    .out({Output, Output_2, Output_3}), .sel(Let));
  Multiplexer #(.select(3), .width(27), .enable("false")) multiplexer_3 (
    .in0({27{1'b0}}), .in1(27'h6022), .in2(27'hc022), .in3(27'hfe80), .in4(27'hfea4), .in5(27'hfe90),
    .out(multiplexer_3_out), .sel(pos_3));  // open: in6, in7
  Multiplexer #(.select(3), .width(27), .enable("false")) multiplexer_4 (
    .in0({27{1'b0}}), .in1(27'h6022), .in2(27'hc022), .in3(27'hfe80), .in4(27'hfea4), .in5(27'hfe90),
    .out(multiplexer_4_out), .sel(pos_2));  // open: in6, in7
  Multiplexer #(.select(3), .width(27), .enable("false")) multiplexer_5 (
    .in0({27{1'b0}}), .in1(27'h3f9f0fe), .in2(27'h3f9f0fe), .in3(27'h4020100), .in4(27'h7fe49ff),
    .in5(27'h5fef97f), .out(multiplexer_5_out), .sel(pos_1));  // open: in6, in7
  Multiplexer #(.select(3), .width(27), .enable("false")) multiplexer_6 (
    .in0({27{1'b0}}), .in1(27'h3f9f0fe), .in2(27'h3f9f0fe), .in3(27'h4020100), .in4(27'h7fe49ff),
    .in5(27'h5fef97f), .out(multiplexer_6_out), .sel(pos_2));  // open: in6, in7
  Multiplexer #(.select(2), .width(27), .enable("false")) multiplexer_7 (
    .in0(multiplexer_5_out), .in1(multiplexer_6_out), .in2(multiplexer_8_out), .in3(multiplexer_8_out),
    .out({Output_4, Output_5, Output_6}), .sel(Let));
  Multiplexer #(.select(3), .width(27), .enable("false")) multiplexer_8 (
    .in0({27{1'b0}}), .in1(27'h3f9f0fe), .in2(27'h3f9f0fe), .in3(27'h4020100), .in4(27'h7fe49ff),
    .in5(27'h5fef97f), .out(multiplexer_8_out), .sel(pos_3));  // open: in6, in7
  Multiplexer #(.select(3), .width(27), .enable("false")) multiplexer_9 (
    .in0({27{1'b0}}), .in1(27'h886000), .in2(27'h88c000), .in3(27'h200fe00), .in4(27'h290fe00),
    .in5(27'h240fe00), .out(multiplexer_9_out), .sel(pos_1));  // open: in6, in7
  Multiplexer #(.select(2), .width(27), .enable("false")) multiplexer_10 (
    .in0(multiplexer_9_out), .in1(multiplexer_12_out), .in2(multiplexer_11_out), .in3(multiplexer_11_out),
    .out({Output_7, Output_8, Output_9}), .sel(Let));
  Multiplexer #(.select(3), .width(27), .enable("false")) multiplexer_11 (
    .in0({27{1'b0}}), .in1(27'h88600), .in2(27'h88c000), .in3(27'h200fe00), .in4(27'h290fe00),
    .in5(27'h240fe00), .out(multiplexer_11_out), .sel(pos_3));  // open: in6, in7
  Multiplexer #(.select(3), .width(27), .enable("false")) multiplexer_12 (
    .in0({27{1'b0}}), .in1(27'h88600), .in2(27'h88c000), .in3(27'h200fe00), .in4(27'h290fe00),
    .in5(27'h240fe00), .out(multiplexer_12_out), .sel(pos_2));  // open: in6, in7

  // Other names for the same wires on the sheet: p1[2:0] = pos_1; p2[2:0] = pos_2; p3[2:0] = pos_3; pict[1:0] = Let
endmodule

module Basic_switch (
  input  [4:0] Let,
  output [8:0] Output,
  output [8:0] Output_2,
  output [8:0] Output_3,
  output [8:0] Output_4,
  output [8:0] Output_5,
  output [8:0] Output_6,
  output [8:0] Output_7,
  output [8:0] Output_8,
  output [8:0] Output_9
);

  Multiplexer #(.select(5), .width(27), .enable("false")) multiplexer_1 (
    .in0({27{1'b0}}), .in1(27'h47e), .in2(27'h104fe), .in3(27'hf8fe), .in4(27'h104fe), .in5(27'h104fe),
    .in6(27'h104fe), .in7(27'hf8fe), .in8(27'h104fe), .in9(27'h18c82), .in10(27'h100e), .in11(27'h104fe),
    .in12(27'h104fe), .in13(27'h1fcfe), .in14(27'h1fcfe), .in15(27'hf8fe), .in16(27'h104fe), .in17(27'hf8fe),
    .in18(27'h1fcfe), .in19(27'hc8f4), .in20(27'h18082), .in21(27'h100fc), .in22(27'h1c018),
    .in23(27'h1f00e), .in24(27'h104c6), .in25(27'h100e0), .in26(27'h1c486), .in27({27{1'b0}}),
    .in28({27{1'b0}}), .in29({27{1'b0}}), .in30({27{1'b0}}), .in31({27{1'b0}}),
    .out({Output, Output_2, Output_3}), .sel(Let));
  Multiplexer #(.select(5), .width(27), .enable("false")) multiplexer_2 (
    .in0({27{1'b0}}), .in1(27'h24124fe), .in2(27'h3f92492), .in3(27'h2090482), .in4(27'h3f90482),
    .in5(27'h3f92492), .in6(27'h3f92490), .in7(27'h209249e), .in8(27'h24820fe), .in9(27'h3f9fc82),
    .in10(27'h30904fe), .in11(27'h3f92430), .in12(27'h3f80402), .in13(27'h882060), .in14(27'h180200c),
    .in15(27'h2090482), .in16(27'h3f91488), .in17(27'h2091086), .in18(27'h2493098), .in19(27'h2492492),
    .in20(27'h3f9fc82), .in21(27'h190cfe), .in22(27'h193cf8), .in23(27'hc0f00c), .in24(27'ha020ee),
    .in25(27'h893cfe), .in26(27'h23924e2), .in27({27{1'b0}}), .in28({27{1'b0}}), .in29({27{1'b0}}),
    .in30({27{1'b0}}), .in31({27{1'b0}}), .out({Output_4, Output_5, Output_6}), .sel(Let));
  Multiplexer #(.select(5), .width(27), .enable("false")) multiplexer_3 (
    .in0({27{1'b0}}), .in1(27'h1f80400), .in2(27'h3f8d800), .in3(27'h318c800), .in4(27'h3f8f800),
    .in5(27'h2098c00), .in6(27'h2018000), .in7(27'h378a000), .in8(27'h3f90400), .in9(27'h3198c00),
    .in10(27'h3f10000), .in11(27'h3790400), .in12(27'h81c00), .in13(27'h3f9fc00), .in14(27'h3f9fc00),
    .in15(27'h3f8f800), .in16(27'h3e0e000), .in17(27'h3f8f400), .in18(27'h3d8c400), .in19(27'h3789800),
    .in20(27'h3018000), .in21(27'h3f10000), .in22(27'h3810000), .in23(27'h3f9f000), .in24(27'h3190400),
    .in25(27'h3890000), .in26(27'h3091c00), .in27({27{1'b0}}), .in28({27{1'b0}}), .in29({27{1'b0}}),
    .in30({27{1'b0}}), .in31({27{1'b0}}), .out({Output_7, Output_8, Output_9}), .sel(Let));
endmodule

module Switch_3_0 (
  input  ctrl,
  input  [4:0] Let,
  input  [4:0] GOLet,
  input  [4:0] WINLet,
  input  reset,
  input  clock,
  input  gen,
  input  Win,
  input  Game_over,
  output [8:0] Output,
  output [8:0] Output_2,
  output [8:0] Output_3,
  output [8:0] Output_4,
  output [8:0] Output_5,
  output [8:0] Output_6,
  output [8:0] Output_7,
  output [8:0] Output_8,
  output [8:0] Output_9
);

  wire comparator_1_eq, fl, multiplexer_1_out, multiplexer_4_out;
  wire [1:1] controlled_buffer_1_out;
  wire [4:0] let_t, multiplexer_3_out;
  wire [7:0] counter_1_q;
  wire [8:0] multiplexer_2_out, multiplexer_2_out_2, multiplexer_2_out_3, multiplexer_5_out,
       multiplexer_5_out_2, multiplexer_5_out_3, multiplexer_6_out, multiplexer_6_out_2, multiplexer_6_out_3;

  Transistor #(.\type ("n"), .width(9)) transistor_1 (.in(multiplexer_2_out_3), .out(Output), .gate(multiplexer_1_out));
  Multiplexer #(.enable("false")) multiplexer_1 (.in0(ctrl), .in1(1'b1), .out(multiplexer_1_out), .sel(fl));
  Counter_part counter_1 (.count(Win), .Q(counter_1_q), .clk(gen));  // open: load, D, carry, clr
  Transistor #(.\type ("n"), .width(9)) transistor_2 (
    .in(multiplexer_2_out_2), .out(Output_2), .gate(multiplexer_1_out));
  Multiplexer #(.select(5), .width(27), .enable("false")) multiplexer_2 (
    .in0({27{1'b0}}), .in1(27'h47e), .in2(27'h104fe), .in3(27'hf8fe), .in4(27'h104fe), .in5(27'h104fe),
    .in6(27'h104fe), .in7(27'hf8fe), .in8(27'h104fe), .in9(27'h18c82), .in10(27'h100e), .in11(27'h104fe),
    .in12(27'h104fe), .in13(27'h1fcfe), .in14(27'h1fcfe), .in15(27'hf8fe), .in16(27'h104fe), .in17(27'hf8fe),
    .in18(27'h1fcfe), .in19(27'hc8f4), .in20(27'h18082), .in21(27'h100fc), .in22(27'h1c018),
    .in23(27'h1f00e), .in24(27'h104c6), .in25(27'h100e0), .in26(27'h1c486), .in27({27{1'b0}}),
    .in28({27{1'b0}}), .in29({27{1'b0}}), .in30({27{1'b0}}), .in31({27{1'b0}}),
    .out({multiplexer_2_out_3, multiplexer_2_out_2, multiplexer_2_out}), .sel(let_t));
  Multiplexer #(.select(2), .width(5), .enable("false")) multiplexer_3 (
    .in0(Let), .in1(GOLet), .in2(WINLet), .in3(WINLet), .out(multiplexer_3_out),
    .sel({controlled_buffer_1_out[1], Game_over}));
  Comparator comparator_1 (.a(counter_1_q), .b({8{1'b1}}), .eq(comparator_1_eq));  // open: gt, lt
  assign controlled_buffer_1_out[1] = comparator_1_eq ? Win : 1'bz;  // Controlled_Buffer controlled_buffer_1
  Pull_Resistor pull_resistor_1 (.node(controlled_buffer_1_out[1]));
  Transistor #(.\type ("n"), .width(9)) transistor_3 (.in(multiplexer_2_out), .out(Output_3), .gate(multiplexer_1_out));
  or or_1 (fl, Game_over, controlled_buffer_1_out[1]);
  Register #(.width(5)) register_1 (
    .D(multiplexer_3_out), .Q(let_t), .clk(multiplexer_4_out), .clr(reset));  // open: en
  Multiplexer #(.enable("false")) multiplexer_4 (.in0(clock), .in1(1'b1), .out(multiplexer_4_out), .sel(fl));
  Transistor #(.\type ("n"), .width(9)) transistor_4 (
    .in(multiplexer_5_out_3), .out(Output_4), .gate(multiplexer_1_out));
  Transistor #(.\type ("n"), .width(9)) transistor_5 (
    .in(multiplexer_5_out_2), .out(Output_5), .gate(multiplexer_1_out));
  Multiplexer #(.select(5), .width(27), .enable("false")) multiplexer_5 (
    .in0({27{1'b0}}), .in1(27'h24124fe), .in2(27'h3f92492), .in3(27'h2090482), .in4(27'h3f90482),
    .in5(27'h3f92492), .in6(27'h3f92490), .in7(27'h209249e), .in8(27'h24820fe), .in9(27'h3f9fc82),
    .in10(27'h30904fe), .in11(27'h3f92430), .in12(27'h3f80402), .in13(27'h882060), .in14(27'h180200c),
    .in15(27'h2090482), .in16(27'h3f91488), .in17(27'h2091086), .in18(27'h2493098), .in19(27'h2492492),
    .in20(27'h3f9fc82), .in21(27'h190cfe), .in22(27'h193cf8), .in23(27'hc0f00c), .in24(27'ha020ee),
    .in25(27'h893cfe), .in26(27'h23924e2), .in27(27'h3e9f400), .in28({27{1'b0}}), .in29({27{1'b0}}),
    .in30({27{1'b0}}), .in31({27{1'b0}}),
    .out({multiplexer_5_out_3, multiplexer_5_out_2, multiplexer_5_out}), .sel(let_t));
  Transistor #(.\type ("n"), .width(9)) transistor_6 (.in(multiplexer_5_out), .out(Output_6), .gate(multiplexer_1_out));
  Transistor #(.\type ("n"), .width(9)) transistor_7 (
    .in(multiplexer_6_out_3), .out(Output_7), .gate(multiplexer_1_out));
  Transistor #(.\type ("n"), .width(9)) transistor_8 (
    .in(multiplexer_6_out_2), .out(Output_8), .gate(multiplexer_1_out));
  Multiplexer #(.select(5), .width(27), .enable("false")) multiplexer_6 (
    .in0({27{1'b0}}), .in1(27'h1f80400), .in2(27'h3f8d800), .in3(27'h318c800), .in4(27'h3f8f800),
    .in5(27'h2098c00), .in6(27'h2018000), .in7(27'h378a000), .in8(27'h3f90400), .in9(27'h3198c00),
    .in10(27'h3f10000), .in11(27'h3790400), .in12(27'h81c00), .in13(27'h3f9fc00), .in14(27'h3f9fc00),
    .in15(27'h3f8f800), .in16(27'h3e0e000), .in17(27'h3f8f400), .in18(27'h3d8c400), .in19(27'h3789800),
    .in20(27'h3018000), .in21(27'h3f10000), .in22(27'h3810000), .in23(27'h3f9f000), .in24(27'h3190400),
    .in25(27'h3890000), .in26(27'h3091c00), .in27({27{1'b0}}), .in28({27{1'b0}}), .in29({27{1'b0}}),
    .in30({27{1'b0}}), .in31({27{1'b0}}),
    .out({multiplexer_6_out_3, multiplexer_6_out_2, multiplexer_6_out}), .sel(let_t));
  Transistor #(.\type ("n"), .width(9)) transistor_9 (.in(multiplexer_6_out), .out(Output_9), .gate(multiplexer_1_out));
  Transistor #(.gate("br"), .width(9)) transistor_10 (.in({9{1'b0}}), .out(Output), .gate(multiplexer_1_out));
  Transistor #(.gate("br"), .width(9)) transistor_11 (.in(9'h7f), .out(Output_2), .gate(multiplexer_1_out));
  Transistor #(.gate("br"), .width(9)) transistor_12 (.in(9'ha4), .out(Output_3), .gate(multiplexer_1_out));
  Transistor #(.gate("br"), .width(9)) transistor_13 (.in({9{1'b1}}), .out(Output_4), .gate(multiplexer_1_out));
  Transistor #(.gate("br"), .width(9)) transistor_14 (.in(9'h124), .out(Output_5), .gate(multiplexer_1_out));
  Transistor #(.gate("br"), .width(9)) transistor_15 (.in({9{1'b1}}), .out(Output_6), .gate(multiplexer_1_out));
  Transistor #(.gate("br"), .width(9)) transistor_16 (.in(9'ha4), .out(Output_7), .gate(multiplexer_1_out));
  Transistor #(.gate("br"), .width(9)) transistor_17 (.in(9'h7f), .out(Output_8), .gate(multiplexer_1_out));
  Transistor #(.gate("br"), .width(9)) transistor_18 (.in({9{1'b0}}), .out(Output_9), .gate(multiplexer_1_out));
endmodule

module Life_cntr (
  input  start,
  input  [7:0] flags,
  input  clock,
  input  reset,
  output [3:0] display,
  output Game_over
);

  wire comparator_1_eq, d_ff_1_q;
  wire [2:0] counter_1_q;
  wire [7:0] register_1_q;

  Register register_1 (.D(flags), .Q(register_1_q), .clk(clock), .clr(reset));  // open: en
  Comparator comparator_1 (.a(flags), .b(register_1_q), .eq(comparator_1_eq));  // open: gt, lt
  Multiplexer #(.width(4), .enable("false")) multiplexer_1 (
    .in0(4'b0001), .in1({1'b0, counter_1_q}), .out(display), .sel(d_ff_1_q));
  D_Flip_Flop d_ff_1 (.clk(start), .D(start), .Q(d_ff_1_q), .reset(reset));  // open: Qn, preset, en
  Counter_part #(.width(3), .max('h7), .ongoal("stay")) counter_1 (
    .count(comparator_1_eq), .Q(counter_1_q), .carry(Game_over), .clk(clock), .clr(reset));  // open: load, D
endmodule

module counter_invertor (
  input  [3:0] \input ,
  output [3:0] \output 
);

  not not_1 (\output [1], \input [1]);
  not not_2 (\output [2], \input [2]);
  not not_3 (\output [0], \input [0]);

  assign \output [3] = \input [3];
endmodule

module Counter (
  input  [7:0] Max,
  input  clock,
  input  reset,
  output \end ,
  output [7:0] out
);

  wire st;
  wire [7:0] inc_1_out;

  Register register_1 (.D(inc_1_out), .en(st), .Q(out), .clk(clock), .clr(reset));
  inc inc_1 (.in(out), .out(inc_1_out));  // open: cout
  Comparator comparator_1 (.a(Max), .b(out), .lt(\end ));  // open: gt, eq
  not not_1 (st, \end );
endmodule

module inc (
  input  [7:0] in,
  output [7:0] out,
  output cout
);

  wire [7:1] and_1_out;

  assign {cout, and_1_out} = {and_1_out, 1'b1} & in;  // AND_Gate and_1, 8 bits wide
  assign out = in ^ {and_1_out, 1'b1};  // XOR_Gate xor_1, 8 bits wide
endmodule

module RAM_adress_controller (
  input  [7:0] proc,
  input  [3:0] word_load,
  input  word_loaded,
  input  halt,
  output [7:0] out
);

  wire [7:0] transistor_1_out, transistor_3_out;

  Transistor #(.\type ("n"), .gate("br"), .width(8)) transistor_1 (
    .in(proc), .out(transistor_1_out), .gate(word_loaded));
  Transistor #(.gate("br"), .width(8)) transistor_2 (.in({4'b0000, word_load}), .out(out), .gate(word_loaded));
  Transistor #(.\type ("n"), .gate("br"), .width(8)) transistor_3 (
    .in(8'h9), .out(transistor_3_out), .gate(word_loaded));
  Transistor #(.gate("br"), .width(8)) transistor_4 (.in(transistor_1_out), .out(out), .gate(halt));
  Transistor #(.\type ("n"), .gate("br"), .width(8)) transistor_5 (.in(transistor_3_out), .out(out), .gate(halt));

  // Notes on the sheet:
  //   letter load
endmodule

module RAM_data_controller (
  input  [7:0] proc,
  input  [4:0] word,
  input  [4:0] letter,
  input  word_loaded,
  input  halt,
  output [7:0] out
);

  wire [7:0] transistor_4_out, transistor_5_out;

  Transistor #(.\type ("n"), .gate("br"), .width(8)) transistor_1 (
    .in(transistor_4_out), .out(out), .gate(word_loaded));
  Transistor #(.gate("br"), .width(8)) transistor_2 (.in({3'b000, word}), .out(out), .gate(word_loaded));
  Transistor #(.\type ("n"), .gate("br"), .width(8)) transistor_3 (
    .in(transistor_5_out), .out(out), .gate(word_loaded));
  Transistor #(.gate("br"), .width(8)) transistor_4 (.in(proc), .out(transistor_4_out), .gate(halt));
  Transistor #(.\type ("n"), .gate("br"), .width(8)) transistor_5 (
    .in({3'b000, letter}), .out(transistor_5_out), .gate(halt));
endmodule

module Alphabet (
);

  DotMatrix #(.matrixcols(9), .matrixrows(9)) dotmatrix_1 (
    .col0({9{1'b0}}), .col1(9'h2), .col2(9'h7e), .col3(9'h90), .col4(9'h92), .col5(9'hfe), .col6(9'h7e),
    .col7(9'h2), .col8({9{1'b0}}));
  DotMatrix #(.matrixcols(9), .matrixrows(9)) dotmatrix_2 (
    .col0({9{1'b0}}), .col1(9'h8), .col2(9'he), .col3(9'hc2), .col4(9'h82), .col5(9'hfe), .col6(9'hfc),
    .col7(9'h80), .col8({9{1'b0}}));
  DotMatrix #(.matrixcols(9), .matrixrows(9)) dotmatrix_3 (
    .col0({9{1'b0}}), .col1(9'h64), .col2(9'hf4), .col3(9'h92), .col4(9'h92), .col5(9'h92), .col6(9'hde),
    .col7(9'h4c), .col8({9{1'b0}}));
  DotMatrix #(.matrixcols(9), .matrixrows(9)) dotmatrix_4 (
    .col0({9{1'b0}}), .col1(9'h82), .col2(9'hfe), .col3(9'hfe), .col4(9'h92), .col5(9'h92), .col6(9'hfe),
    .col7(9'h6c), .col8({9{1'b0}}));
  DotMatrix #(.matrixcols(9), .matrixrows(9)) dotmatrix_5 (
    .col0({9{1'b0}}), .col1(9'h82), .col2(9'hfe), .col3(9'hfe), .col4(9'h92), .col5(9'h30), .col6(9'hde),
    .col7(9'h82), .col8({9{1'b0}}));
  DotMatrix #(.matrixcols(9), .matrixrows(9)) dotmatrix_6 (
    .col0({9{1'b0}}), .col1(9'hc0), .col2(9'h82), .col3(9'hfe), .col4(9'hfe), .col5(9'h82), .col6(9'hc0),
    .col7(9'hc0), .col8({9{1'b0}}));
  DotMatrix #(.matrixcols(9), .matrixrows(9)) dotmatrix_7 (
    .col0({9{1'b0}}), .col1(9'h7c), .col2(9'hfe), .col3(9'h82), .col4(9'h82), .col5(9'h82), .col6(9'hc6),
    .col7(9'h64), .col8({9{1'b0}}));
  DotMatrix #(.matrixcols(9), .matrixrows(9)) dotmatrix_8 (
    .col0({9{1'b0}}), .col1(9'h82), .col2(9'hfe), .col3(9'hfe), .col4(9'h2), .col5(9'h2), .col6(9'h2),
    .col7(9'he), .col8({9{1'b0}}));
  DotMatrix #(.matrixcols(9), .matrixrows(9)) dotmatrix_9 (
    .col0({9{1'b0}}), .col1(9'h80), .col2(9'hfc), .col3(9'h6), .col4(9'h86), .col5(9'hfe), .col6(9'hfc),
    .col7(9'h80), .col8({9{1'b0}}));
  DotMatrix #(.matrixcols(9), .matrixrows(9)) dotmatrix_10 (
    .col0({9{1'b0}}), .col1({9{1'b0}}), .col2({9{1'b0}}), .col3({9{1'b0}}), .col4(9'hfa), .col5(9'hfa),
    .col6({9{1'b0}}), .col7({9{1'b0}}), .col8({9{1'b0}}));
  DotMatrix #(.matrixcols(9), .matrixrows(9)) dotmatrix_11 (
    .col0({9{1'b0}}), .col1(9'h82), .col2(9'hfe), .col3(9'hfe), .col4(9'h82), .col5(9'h82), .col6(9'hfe),
    .col7(9'h7c), .col8({9{1'b0}}));
  DotMatrix #(.matrixcols(9), .matrixrows(9)) dotmatrix_12 (
    .col0({9{1'b0}}), .col1(9'hfe), .col2(9'hfe), .col3(9'h22), .col4(9'h10), .col5(9'h60), .col6(9'hfe),
    .col7(9'hfe), .col8({9{1'b0}}));
  DotMatrix #(.matrixcols(9), .matrixrows(9)) dotmatrix_13 (
    .col0({9{1'b0}}), .col1(9'he0), .col2(9'h18), .col3(9'h6), .col4(9'h9e), .col5(9'hf8), .col6(9'he0),
    .col7(9'h80), .col8({9{1'b0}}));
  DotMatrix #(.matrixcols(9), .matrixrows(9)) dotmatrix_14 (
    .col0({9{1'b0}}), .col1(9'h30), .col2(9'h22), .col3(9'hfe), .col4(9'hf8), .col5(9'hfe), .col6(9'h22),
    .col7(9'h30), .col8({9{1'b0}}));
  DotMatrix #(.matrixcols(9), .matrixrows(9)) dotmatrix_15 (
    .col0({9{1'b0}}), .col1(9'h82), .col2(9'hfe), .col3(9'hfe), .col4(9'h92), .col5(9'h92), .col6(9'h82),
    .col7(9'hc6), .col8({9{1'b0}}));
  DotMatrix #(.matrixcols(9), .matrixrows(9)) dotmatrix_16 (
    .col0({9{1'b0}}), .col1(9'hfe), .col2(9'hfe), .col3(9'h60), .col4(9'h10), .col5(9'hc), .col6(9'hfe),
    .col7(9'hfe), .col8({9{1'b0}}));
  DotMatrix #(.matrixcols(9), .matrixrows(9)) dotmatrix_17 (
    .col0({9{1'b0}}), .col1(9'hf8), .col2(9'he), .col3(9'h30), .col4(9'h78), .col5(9'hc), .col6(9'hfe),
    .col7(9'hf8), .col8({9{1'b0}}));
  DotMatrix #(.matrixcols(9), .matrixrows(9)) dotmatrix_18 (
    .col0({9{1'b0}}), .col1(9'h60), .col2(9'h22), .col3(9'hfe), .col4(9'hf8), .col5(9'hfe), .col6(9'h22),
    .col7(9'h60), .col8({9{1'b0}}));
  DotMatrix #(.matrixcols(9), .matrixrows(9)) dotmatrix_19 (
    .col0({9{1'b0}}), .col1(9'h82), .col2(9'hfe), .col3(9'hfe), .col4(9'h92), .col5(9'h90), .col6(9'h80),
    .col7(9'hc0), .col8({9{1'b0}}));
  DotMatrix #(.matrixcols(9), .matrixrows(9)) dotmatrix_20 (
    .col0({9{1'b0}}), .col1(9'h7c), .col2(9'hfe), .col3(9'h82), .col4(9'h82), .col5(9'h82), .col6(9'hfe),
    .col7(9'h7c), .col8({9{1'b0}}));
  DotMatrix #(.matrixcols(9), .matrixrows(9)) dotmatrix_21 (
    .col0({9{1'b0}}), .col1(9'h82), .col2(9'hc6), .col3(9'h28), .col4(9'h10), .col5(9'hee), .col6(9'hc6),
    .col7(9'h82), .col8({9{1'b0}}));
  DotMatrix #(.matrixcols(9), .matrixrows(9)) dotmatrix_22 (
    .col0({9{1'b0}}), .col1(9'h30), .col2(9'h20), .col3(9'hfe), .col4(9'hf8), .col5(9'hfe), .col6(9'h22),
    .col7(9'h20), .col8({9{1'b0}}));
  DotMatrix #(.matrixcols(9), .matrixrows(9)) dotmatrix_23 (
    .col0({9{1'b0}}), .col1(9'h7c), .col2(9'hfe), .col3(9'h82), .col4(9'h92), .col5(9'h9e), .col6(9'hde),
    .col7(9'h50), .col8({9{1'b0}}));
  DotMatrix #(.matrixcols(9), .matrixrows(9)) dotmatrix_24 (
    .col0({9{1'b0}}), .col1(9'h82), .col2(9'hfe), .col3(9'hfe), .col4(9'h8a), .col5(9'h88), .col6(9'hf8),
    .col7(9'h70), .col8({9{1'b0}}));
  DotMatrix #(.matrixcols(9), .matrixrows(9)) dotmatrix_25 (
    .col0({9{1'b0}}), .col1(9'h80), .col2(9'he0), .col3(9'h22), .col4(9'h9e), .col5(9'hfe), .col6(9'he2),
    .col7(9'h80), .col8({9{1'b0}}));
  DotMatrix #(.matrixcols(9), .matrixrows(9)) dotmatrix_26 (
    .col0({9{1'b1}}), .col1(9'h118), .col2(9'h110), .col3(9'h17f), .col4(9'h17c), .col5(9'h17f),
    .col6(9'h111), .col7(9'h110), .col8({9{1'b1}}));
  DotMatrix #(.matrixcols(9), .matrixrows(9)) dotmatrix_27 (
    .col0({9{1'b0}}), .col1(9'h82), .col2(9'hfe), .col3(9'h92), .col4(9'h10), .col5(9'hfe), .col6(9'hfe),
    .col7(9'h82), .col8({9{1'b0}}));
  DotMatrix #(.matrixcols(9), .matrixrows(9)) dotmatrix_28 (
    .col0({9{1'b0}}), .col1(9'h7c), .col2(9'hfe), .col3(9'h82), .col4(9'h88), .col5(9'h86), .col6(9'hfe),
    .col7(9'h7a), .col8({9{1'b0}}));
  DotMatrix #(.matrixcols(9), .matrixrows(9)) dotmatrix_29 (
    .col0({9{1'b0}}), .col1(9'he2), .col2(9'h86), .col3(9'h8e), .col4(9'h92), .col5(9'he2), .col6(9'hc2),
    .col7(9'h8e), .col8({9{1'b0}}));
  DotMatrix #(.matrixcols(9), .matrixrows(9)) dotmatrix_30 (
    .col0({9{1'b0}}), .col1(9'h7f), .col2(9'h80), .col3(9'h100), .col4(9'h100), .col5(9'h100), .col6(9'h80),
    .col7(9'h7f), .col8({9{1'b0}}));
  DotMatrix #(.matrixcols(9), .matrixrows(9)) dotmatrix_31 (
    .col0({9{1'b0}}), .col1(9'hc6), .col2(9'h82), .col3(9'hfe), .col4(9'hfe), .col5(9'h82), .col6(9'hc6),
    .col7(9'hc6), .col8({9{1'b0}}));
  DotMatrix #(.matrixcols(9), .matrixrows(9)) dotmatrix_32 (
    .col0({9{1'b0}}), .col1(9'hfe), .col2(9'hfe), .col3(9'h92), .col4(9'h98), .col5(9'h98), .col6(9'hf6),
    .col7(9'h62), .col8({9{1'b0}}));
  DotMatrix #(.matrixcols(9), .matrixrows(9)) dotmatrix_33 (
    .col0({9{1'b0}}), .col1(9'h7f), .col2(9'ha4), .col3({9{1'b1}}), .col4(9'h124), .col5({9{1'b1}}),
    .col6(9'ha4), .col7(9'h7f), .col8({9{1'b0}}));
  DotMatrix #(.matrixcols(9), .matrixrows(9)) dotmatrix_34 (
    .col0({9{1'b0}}), .col1(9'h7f), .col2(9'h90), .col3(9'h17f), .col4(9'h17c), .col5(9'h17f), .col6(9'h90),
    .col7(9'h7f), .col8({9{1'b0}}));
endmodule

module answers (
);


  // Notes on the sheet:
  //   50) FESTIVAL; DISCOVER
  //   70) GENERATE; BEAUTIFY
  //   80) BUILDING; CHILDREN
  //   90) HOSPITAL; KITCHEN
  //   a0) LANGUAGE; MISTAKES
  //   b0) NOTEBOOK; PAINTING
  //   c0) QUESTION; RECEARCH
  //   d0)SOFTWARE; STRATEGY
  //   e0)TRAINING; VACATION
  //   d0)ACTIVITY; STUDENTS
  //   00) ABSOLUTE; CALENDAR
  //   10) ELEPHANT; MOUNTAIN
  //   20) PARADISE; ULTIMATE 
  //   30) DOCUMENT; XENOPHOB
  //   40) COMPUTER; ENGINEER
  //   60) NAVIGATE; OPERATOR
endmodule

module Switch_addition (
  input  fl,
  input  [4:0] \let ,
  input  [8:0] \input ,
  input  [8:0] input_2,
  input  [8:0] input_3,
  input  [8:0] input_4,
  input  [8:0] input_5,
  input  [8:0] input_6,
  input  [8:0] input_7,
  input  [8:0] input_8,
  input  [8:0] input_9,
  output [8:0] input_10,
  output [8:0] input_11,
  output [8:0] input_12,
  output [8:0] input_13,
  output [8:0] input_14,
  output [8:0] input_15,
  output [8:0] input_16,
  output [8:0] input_17,
  output [8:0] input_18
);

  wire [8:0] basic_switch_1_output, basic_switch_1_output_2, basic_switch_1_output_3,
       basic_switch_1_output_4, basic_switch_1_output_5, basic_switch_1_output_6, basic_switch_1_output_7,
       basic_switch_1_output_8, basic_switch_1_output_9;

  Basic_switch basic_switch_1 (
    .Let(\let ), .Output(basic_switch_1_output), .Output_2(basic_switch_1_output_2),
    .Output_3(basic_switch_1_output_3), .Output_4(basic_switch_1_output_4),
    .Output_5(basic_switch_1_output_5), .Output_6(basic_switch_1_output_6),
    .Output_7(basic_switch_1_output_7), .Output_8(basic_switch_1_output_8), .Output_9(basic_switch_1_output_9));
  Multiplexer #(.width(9), .enable("false")) multiplexer_1 (
    .in0(basic_switch_1_output), .in1(\input ), .out(input_10), .sel(fl));
  Multiplexer #(.width(9), .enable("false")) multiplexer_2 (
    .in0(basic_switch_1_output_2), .in1(input_2), .out(input_11), .sel(fl));
  Multiplexer #(.width(9), .enable("false")) multiplexer_3 (
    .in0(basic_switch_1_output_3), .in1(input_3), .out(input_12), .sel(fl));
  Multiplexer #(.width(9), .enable("false")) multiplexer_4 (
    .in0(basic_switch_1_output_4), .in1(input_4), .out(input_13), .sel(fl));
  Multiplexer #(.width(9), .enable("false")) multiplexer_5 (
    .in0(basic_switch_1_output_5), .in1(input_5), .out(input_14), .sel(fl));
  Multiplexer #(.width(9), .enable("false")) multiplexer_6 (
    .in0(basic_switch_1_output_6), .in1(input_6), .out(input_15), .sel(fl));
  Multiplexer #(.width(9), .enable("false")) multiplexer_7 (
    .in0(basic_switch_1_output_7), .in1(input_7), .out(input_16), .sel(fl));
  Multiplexer #(.width(9), .enable("false")) multiplexer_8 (
    .in0(basic_switch_1_output_8), .in1(input_8), .out(input_17), .sel(fl));
  Multiplexer #(.width(9), .enable("false")) multiplexer_9 (
    .in0(basic_switch_1_output_9), .in1(input_9), .out(input_18), .sel(fl));
endmodule

module Tact_divider (
  input  clock,
  output out
);

  wire t_ff_1_q, t_ff_2_q, t_ff_3_q, t_ff_4_q, t_ff_5_q, t_ff_6_q;

  T_Flip_Flop t_ff_1 (.clk(t_ff_2_q), .T(t_ff_2_q), .Q(t_ff_1_q));  // open: Qn, preset, reset, en
  T_Flip_Flop t_ff_2 (.clk(clock), .T(clock), .Q(t_ff_2_q));  // open: Qn, preset, reset, en
  T_Flip_Flop t_ff_3 (.clk(t_ff_1_q), .T(t_ff_1_q), .Q(t_ff_3_q));  // open: Qn, preset, reset, en
  T_Flip_Flop t_ff_4 (.clk(t_ff_3_q), .T(t_ff_3_q), .Q(t_ff_4_q));  // open: Qn, preset, reset, en
  T_Flip_Flop t_ff_5 (.clk(t_ff_4_q), .T(t_ff_4_q), .Q(t_ff_5_q));  // open: Qn, preset, reset, en
  T_Flip_Flop t_ff_6 (.clk(t_ff_5_q), .T(t_ff_5_q), .Q(t_ff_6_q));  // open: Qn, preset, reset, en
  T_Flip_Flop t_ff_7 (.clk(t_ff_6_q), .T(t_ff_6_q), .Q(out));  // open: Qn, preset, reset, en
endmodule
